// Logisim project Assignment_CS23I1027.circ as structural Verilog: 3 circuits, main circuit main
module main (
  input  in_1,
  input  in_2
);

  wire and_1_out, and_2_out, clock_1_out, cs23i1027_1_a, cs23i1027_1_b, cs23i1027_1_c, cs23i1027_1_d,
       cs23i1027_1_e, cs23i1027_1_f, cs23i1027_1_g, j_k_ff_4_qn, or_1_out;
  wire [3:0] j_k_ff_1_q;

  Clock clock_1 (.out(clock_1_out));
  J_K_Flip_Flop j_k_ff_1 (
    .J(j_k_ff_4_qn), .K(j_k_ff_4_qn), .clk(clock_1_out), .Q(j_k_ff_1_q[0]), .preset(in_1), .reset(in_2));  // open: Qn
  J_K_Flip_Flop j_k_ff_2 (
    .J(j_k_ff_1_q[0]), .K(j_k_ff_1_q[0]), .clk(clock_1_out), .Q(j_k_ff_1_q[1]), .preset(in_1), .reset(in_2));  // open: Qn
  and and_1 (and_1_out, j_k_ff_1_q[0], j_k_ff_1_q[1]);
  J_K_Flip_Flop j_k_ff_3 (
    .J(and_1_out), .K(and_1_out), .clk(clock_1_out), .Q(j_k_ff_1_q[2]), .preset(in_1), .reset(in_2));  // open: Qn
  and and_2 (and_2_out, and_1_out, j_k_ff_1_q[2]);
  or or_1 (or_1_out, j_k_ff_1_q[3], and_2_out);
  J_K_Flip_Flop j_k_ff_4 (
    .J(or_1_out), .K(or_1_out), .clk(clock_1_out), .Q(j_k_ff_1_q[3]), .Qn(j_k_ff_4_qn), .preset(in_1),
    .reset(in_2));
  CS23I1027 cs23i1027_1 (
    .Q0(j_k_ff_1_q[3]), .Q1(j_k_ff_1_q[2]), .Q2(j_k_ff_1_q[1]), .Q3(j_k_ff_1_q[0]), .a(cs23i1027_1_a),
    .b(cs23i1027_1_b), .c(cs23i1027_1_c), .d(cs23i1027_1_d), .e(cs23i1027_1_e), .f(cs23i1027_1_f),
    .g(cs23i1027_1_g));
  Hex_Digit_Display hex_digit_display_1 (.value(j_k_ff_1_q));  // open: dp
  _7_Segment_Display u_7_segment_display_1 (
    .g(cs23i1027_1_g), .f(cs23i1027_1_f), .a(cs23i1027_1_a), .b(cs23i1027_1_b), .e(cs23i1027_1_e),
    .d(cs23i1027_1_d), .c(cs23i1027_1_c));  // open: dp
endmodule

module CS23I1027_Not_Working (
  input  Q3,
  input  Q2,
  input  Q1,
  input  Q0,
  output a,
  output b,
  output c,
  output d,
  output e,
  output f,
  output g
);

  wire and_1_out, and_2_out, and_3_out, and_4_out, and_5_out, and_6_out, and_7_out, and_8_out, and_9_out,
       and_10_out, and_11_out, and_12_out, and_13_out, and_14_out, and_15_out, and_16_out, and_17_out,
       and_18_out, and_19_out, and_20_out, and_21_out, and_22_out, and_23_out, and_24_out, not_1_out,
       not_2_out, not_3_out, not_4_out;

  not not_1 (not_1_out, Q3);
  not not_2 (not_2_out, Q2);
  not not_3 (not_3_out, Q1);
  not not_4 (not_4_out, Q0);
  and and_1 (and_1_out, not_1_out, Q2, Q1);
  and and_2 (and_2_out, not_1_out, Q2, not_4_out);
  and and_3 (and_3_out, Q3, not_2_out, Q1);
  and and_4 (and_4_out, Q3, not_3_out, Q0);
  and and_5 (and_5_out, not_2_out, Q2, not_3_out);
  and and_6 (and_6_out, not_1_out, not_2_out, Q1);
  and and_7 (and_7_out, not_1_out, Q2, Q0);
  and and_8 (and_8_out, Q3, not_3_out, Q0);
  and and_9 (and_9_out, not_1_out, Q2);
  and and_10 (and_10_out, Q3, not_2_out, Q0);
  and and_11 (and_11_out, Q3, not_2_out, not_3_out);
  and and_12 (and_12_out, not_1_out, not_3_out);
  and and_13 (and_13_out, not_1_out, not_2_out, Q1);
  and and_14 (and_14_out, not_1_out, Q2, Q0);
  and and_15 (and_15_out, Q3, not_2_out, Q1);
  and and_16 (and_16_out, Q3, not_3_out, Q0);
  and and_17 (and_17_out, not_1_out, Q1);
  and and_18 (and_18_out, Q3, not_2_out, not_4_out);
  and and_19 (and_19_out, not_1_out, Q2);
  and and_20 (and_20_out, not_1_out, not_2_out, Q0);
  and and_21 (and_21_out, Q3, not_2_out, not_3_out);
  and and_22 (and_22_out, not_1_out, not_2_out, Q1);
  and and_23 (and_23_out, not_1_out, Q2, Q0);
  and and_24 (and_24_out, Q3, not_2_out, not_3_out);
  or or_1 (a, and_1_out, and_2_out, and_3_out, and_4_out);
  or or_2 (b, and_5_out, and_6_out, and_7_out, and_8_out);
  or or_3 (c, and_9_out, and_10_out, and_11_out, and_12_out);
  or or_4 (d, and_13_out, and_14_out, and_15_out, and_16_out);
  or or_5 (e, and_17_out, and_18_out);
  or or_6 (f, and_19_out, and_20_out, and_21_out);
  or or_7 (g, and_22_out, and_23_out, and_24_out);
endmodule

module CS23I1027 (
  input  Q0,
  input  Q1,
  input  Q2,
  input  Q3,
  output a,
  output b,
  output c,
  output d,
  output e,
  output f,
  output g
);

  wire and_1_out, and_2_out, and_3_out, and_4_out, and_5_out, and_6_out, and_7_out, and_8_out, and_9_out,
       not_1_out, not_2_out, not_3_out, not_4_out, xor_1_out;

  not not_1 (not_1_out, Q0);
  not not_2 (not_2_out, Q1);
  not not_3 (not_3_out, Q2);
  not not_4 (not_4_out, Q3);
  and and_1 (and_1_out, not_1_out, not_2_out, not_4_out);
  and and_2 (and_2_out, not_4_out, Q2, Q1);
  and and_3 (and_3_out, Q1, not_3_out);
  xor xor_1 (xor_1_out, Q1, Q3);
  and and_4 (and_4_out, not_1_out, not_2_out);
  and and_5 (and_5_out, Q2, Q1);
  and and_6 (and_6_out, not_1_out, not_3_out, not_2_out);
  and and_7 (and_7_out, not_2_out, Q2);
  and and_8 (and_8_out, not_2_out, Q3);
  and and_9 (and_9_out, Q2, Q3);
  or or_1 (a, not_2_out, Q2);
  or or_2 (b, Q0, Q1, Q2);
  or or_3 (c, Q0, and_3_out, xor_1_out);
  or or_4 (d, and_4_out, Q2);
  or or_5 (e, and_5_out, and_1_out);
  or or_6 (f, and_6_out, and_2_out);
  or or_7 (g, and_7_out, and_8_out, and_9_out);
endmodule
