// Logisim project Hardware_EndSemQ1.circ as structural Verilog: 4 circuits, main circuit main
module main (
  input  K1,
  input  K0,
  input  in_3,
  input  in_4,
  input  in_5,
  input  in_6,
  input  in_7,
  input  in_8,
  input  in_9,
  output out_10,
  output out_11,
  output out_12,
  output S2,
  output S1,
  output S0,
  output D2,
  output D1,
  output D0,
  output A2,
  output A1,
  output A0,
  output out_22,
  output out_23,
  output out_24
);

  wire and_1_out, and_2_out, and_3_out, and_4_out, and_5_out, and_6_out, and_7_out, and_8_out, and_9_out,
       and_10_out, and_11_out, and_12_out, and_13_out, clock_1_out, not_1_out, not_2_out, not_3_out,
       not_4_out, not_5_out, not_6_out, or_1_out, or_2_out, t_ff_1_q, t_ff_2_qn, twobitadder_1_c,
       twobitsubtr_1_b;
  wire [1:0] t_ff_3_q;

  or or_1 (or_1_out, and_1_out, t_ff_1_q);
  T_Flip_Flop t_ff_1 (.T(or_1_out), .clk(clock_1_out), .Q(t_ff_1_q));  // open: Qn, reset, preset
  Clock clock_1 (.out(clock_1_out));
  or or_2 (or_2_out, t_ff_2_qn, t_ff_1_q);
  T_Flip_Flop t_ff_2 (.T(or_2_out), .clk(clock_1_out), .Q(t_ff_3_q[1]), .Qn(t_ff_2_qn));  // open: reset, preset
  and and_1 (and_1_out, t_ff_3_q[1], t_ff_3_q[0]);
  T_Flip_Flop t_ff_3 (.T(in_5), .clk(clock_1_out), .Q(t_ff_3_q[0]));  // open: Qn, reset, preset
  Hex_Digit_Display hex_digit_display_1 (.value({{2{in_4}}, t_ff_3_q}));  // open: dp
  xor xor_1 (A1, K0, t_ff_3_q[0]);
  xor xor_2 (A0, K1, t_ff_3_q[1]);
  TwoBitAdder twobitadder_1 (.X(K0), .Y(t_ff_3_q[0]), .Cin(in_6), .S(S0), .C(twobitadder_1_c));
  TwoBitSubtr twobitsubtr_1 (.X(K0), .Y(t_ff_3_q[0]), .Cin(in_6), .D(D0), .B(twobitsubtr_1_b));
  TwoBitAdder twobitadder_2 (.X(K1), .Y(t_ff_3_q[1]), .Cin(twobitadder_1_c), .S(S1), .C(S2));
  TwoBitSubtr twobitsubtr_2 (.X(K1), .Y(t_ff_3_q[1]), .Cin(twobitsubtr_1_b), .D(D1), .B(D2));
  not not_1 (not_1_out, t_ff_3_q[1]);
  not not_2 (not_2_out, t_ff_3_q[1]);
  not not_3 (not_3_out, t_ff_3_q[1]);
  not not_4 (not_4_out, t_ff_3_q[0]);
  not not_5 (not_5_out, t_ff_3_q[0]);
  not not_6 (not_6_out, t_ff_3_q[0]);
  and and_2 (and_2_out, not_4_out, not_1_out, in_7);
  and and_3 (and_3_out, t_ff_3_q[0], not_1_out, S1);
  and and_4 (and_4_out, not_4_out, t_ff_3_q[1], D1);
  and and_5 (and_5_out, t_ff_3_q[0], t_ff_3_q[1], A1);
  and and_6 (and_6_out, not_5_out, not_2_out, in_9);
  and and_7 (and_7_out, t_ff_3_q[0], not_2_out, S0);
  and and_8 (and_8_out, not_5_out, t_ff_3_q[1], D0);
  and and_9 (and_9_out, t_ff_3_q[0], t_ff_3_q[1], A0);
  and and_10 (and_10_out, not_6_out, not_3_out, in_3);
  and and_11 (and_11_out, t_ff_3_q[0], not_3_out, S2);
  and and_12 (and_12_out, not_6_out, t_ff_3_q[1], D2);
  and and_13 (and_13_out, t_ff_3_q[0], t_ff_3_q[1], in_8);
  or or_3 (out_10, and_10_out, and_11_out, and_12_out, and_13_out);
  or or_4 (out_11, and_2_out, and_3_out, and_4_out, and_5_out);
  or or_5 (out_12, and_6_out, and_7_out, and_8_out, and_9_out);

  assign A2 = in_8;
  assign out_22 = out_10;
  assign out_23 = out_11;
  assign out_24 = out_12;
endmodule

module TwoBitAdder (
  input  X,
  input  Y,
  input  Cin,
  output S,
  output C
);

  wire and_1_out, and_2_out, xor_1_out;

  xor xor_1 (xor_1_out, X, Y);
  and and_1 (and_1_out, X, Y);
  xor xor_2 (S, xor_1_out, Cin);
  and and_2 (and_2_out, xor_1_out, Cin);
  or or_1 (C, and_2_out, and_1_out);
endmodule

module TwoBitSubtr (
  input  X,
  input  Y,
  input  Cin,
  output D,
  output B
);

  wire and_1_out, and_2_out, and_3_out, not_1_out, xor_1_out;

  not not_1 (not_1_out, X);
  xor xor_1 (xor_1_out, X, Y);
  and and_1 (and_1_out, not_1_out, Y);
  xor xor_2 (D, xor_1_out, Cin);
  and and_2 (and_2_out, not_1_out, Cin);
  and and_3 (and_3_out, Cin, Y);
  or or_1 (B, and_2_out, and_3_out, and_1_out);
endmodule

module FourToOneMult (
  input  Q1,
  input  Q0,
  input  I0,
  input  I1,
  input  I2,
  input  I3,
  output R
);

  wire and_1_out, and_2_out, and_3_out, and_4_out, not_1_out, not_2_out;

  not not_1 (not_1_out, Q1);
  not not_2 (not_2_out, Q0);
  and and_1 (and_1_out, not_2_out, not_1_out, I0);
  and and_2 (and_2_out, Q0, not_1_out, I1);
  and and_3 (and_3_out, not_2_out, Q1, I2);
  and and_4 (and_4_out, Q0, Q1, I3);
  or or_1 (R, and_1_out, and_2_out, and_3_out, and_4_out);
endmodule
