// Logisim project Q1.circ as structural Verilog: 1 circuit, main circuit main
module main (
  input  A,
  input  B,
  input  C,
  output out_4
);

  wire ABC_out, ABpCp_out, ApBC_out, ApBp_out, ApBpC_out, BC_out, BpCp_out, not_1_out, not_2_out, not_3_out,
       or_1_out, or_2_out;

  not not_1 (not_1_out, A);
  not not_2 (not_2_out, B);
  not not_3 (not_3_out, C);
  and ApBp (ApBp_out, not_1_out, not_2_out);
  and BC (BC_out, B, C);
  and BpCp (BpCp_out, not_2_out, not_3_out);
  and ABC (ABC_out, A, BC_out);
  and ApBC (ApBC_out, not_1_out, BC_out);
  and ApBpC (ApBpC_out, ApBp_out, C);
  and ABpCp (ABpCp_out, A, BpCp_out);
  or or_1 (or_1_out, ABC_out, ApBC_out);
  or or_2 (or_2_out, ApBpC_out, ABpCp_out);
  or or_3 (out_4, or_1_out, or_2_out);
endmodule
