// Logisim project Q3.circ as structural Verilog: 1 circuit, main circuit main
module main (
  input  A,
  input  B,
  input  C,
  output out_4
);

  wire AB_out, ABC_out, and_1_out, and_2_out, BC_out, not_1_out, not_2_out, not_3_out, or_1_out, or_2_out;

  not not_1 (not_1_out, A);
  not not_2 (not_2_out, B);
  not not_3 (not_3_out, C);
  and AB (AB_out, A, B);
  and BC (BC_out, B, C);
  and ABC (ABC_out, AB_out, C);
  and and_1 (and_1_out, not_1_out, not_2_out);
  and and_2 (and_2_out, and_1_out, not_3_out);
  or or_1 (or_1_out, AB_out, BC_out);
  or or_2 (or_2_out, or_1_out, ABC_out);
  or or_3 (out_4, and_2_out, or_2_out);
endmodule
