// Logisim project FullCycleCounterIncrementer_Asynch.circ as structural Verilog: 1 circuit, main circuit main
module main (
  input  in_1,
  input  Set1,
  input  Set2,
  input  in_4,
  input  in_5,
  input  Reset1,
  input  Reset2
);

  wire and_1_out, and_2_out, and_3_out, and_4_out, Clk_out, not_1_out, not_2_out, not_3_out;
  wire [2:0] t_ff_1_q;
  wire [3:0] t_ff_4_q;

  Clock Clk (.out(Clk_out));
  T_Flip_Flop t_ff_1 (.T(in_4), .clk(Clk_out), .Q(t_ff_1_q[0]), .reset(Reset1), .preset(Set1));  // open: Qn
  T_Flip_Flop t_ff_2 (.T(t_ff_1_q[0]), .clk(Clk_out), .Q(t_ff_1_q[1]), .reset(Reset1), .preset(Set1));  // open: Qn
  and and_1 (and_1_out, t_ff_1_q[0], t_ff_1_q[1]);
  T_Flip_Flop t_ff_3 (.T(and_1_out), .clk(Clk_out), .Q(t_ff_1_q[2]), .reset(Reset1), .preset(Set1));  // open: Qn
  not not_1 (not_1_out, t_ff_1_q[0]);
  not not_2 (not_2_out, t_ff_1_q[1]);
  not not_3 (not_3_out, t_ff_1_q[2]);
  Hex_Digit_Display hex_digit_display_1 (.value({in_1, t_ff_1_q}));  // open: dp
  and and_2 (and_2_out, not_1_out, not_2_out, not_3_out);
  T_Flip_Flop t_ff_4 (.T(in_5), .clk(and_2_out), .Q(t_ff_4_q[0]), .reset(Reset2), .preset(Set2));  // open: Qn
  T_Flip_Flop t_ff_5 (.T(t_ff_4_q[0]), .clk(and_2_out), .Q(t_ff_4_q[1]), .reset(Reset2), .preset(Set2));  // open: Qn
  Hex_Digit_Display hex_digit_display_2 (.value(t_ff_4_q));  // open: dp
  and and_3 (and_3_out, t_ff_4_q[0], t_ff_4_q[1]);
  T_Flip_Flop t_ff_6 (.T(and_3_out), .clk(and_2_out), .Q(t_ff_4_q[2]), .reset(Reset2), .preset(Set2));  // open: Qn
  and and_4 (and_4_out, and_3_out, t_ff_4_q[2]);
  T_Flip_Flop t_ff_7 (.T(and_4_out), .clk(and_2_out), .Q(t_ff_4_q[3]), .reset(Reset2));  // open: Qn, preset
endmodule
