// Logisim project FullCycleCounterIncrementer_Synch.circ as structural Verilog: 1 circuit, main circuit main
module main (
  input  PlayOrPause,
  input  in_2,
  input  Reset
);

  wire and_1_out, and_2_out, and_3_out, and_4_out, and_5_out, and_6_out, Clk_out, not_1_out;
  wire [2:0] t_ff_6_q;
  wire [3:0] t_ff_7_q;

  Clock Clk (.out(Clk_out));
  not not_1 (not_1_out, PlayOrPause);
  and and_1 (and_1_out, t_ff_6_q[1], and_3_out);
  and and_2 (and_2_out, t_ff_7_q[2], and_4_out);
  T_Flip_Flop t_ff_1 (.T(and_1_out), .clk(Clk_out), .Q(t_ff_6_q[2]), .reset(Reset));  // open: Qn, preset
  T_Flip_Flop t_ff_2 (.T(and_2_out), .clk(Clk_out), .Q(t_ff_7_q[3]), .reset(Reset));  // open: Qn, preset
  and and_3 (and_3_out, t_ff_6_q[0], not_1_out);
  and and_4 (and_4_out, t_ff_7_q[1], and_6_out);
  T_Flip_Flop t_ff_3 (.T(and_4_out), .clk(Clk_out), .Q(t_ff_7_q[2]), .reset(Reset));  // open: Qn, preset
  T_Flip_Flop t_ff_4 (.T(and_3_out), .clk(Clk_out), .Q(t_ff_6_q[1]), .reset(Reset));  // open: Qn, preset
  and and_5 (and_5_out, and_1_out, t_ff_6_q[2]);
  and and_6 (and_6_out, t_ff_7_q[0], and_5_out);
  T_Flip_Flop t_ff_5 (.T(and_6_out), .clk(Clk_out), .Q(t_ff_7_q[1]), .reset(Reset));  // open: Qn, preset
  T_Flip_Flop t_ff_6 (.T(not_1_out), .clk(Clk_out), .Q(t_ff_6_q[0]), .reset(Reset));  // open: Qn, preset
  T_Flip_Flop t_ff_7 (.T(and_5_out), .clk(Clk_out), .Q(t_ff_7_q[0]), .reset(Reset));  // open: Qn, preset
  Hex_Digit_Display hex_digit_display_1 (.value({in_2, t_ff_6_q}));  // open: dp
  Hex_Digit_Display hex_digit_display_2 (.value(t_ff_7_q));  // open: dp
endmodule
