// Logisim project HalfCycleCounterIncrementer_Synchr_Harie.circ as structural Verilog: 1 circuit, main circuit main
module main (
  input  PlayOrPause,
  input  Reset,
  input  in_3,
  output [3:0] out_4,
  output [3:0] out_5
);

  wire and_1_out, and_2_out, and_3_out, and_4_out, and_5_out, and_6_out, and_7_out, Clk_out, not_1_out;

  Clock Clk (.out(Clk_out));
  not not_1 (not_1_out, PlayOrPause);
  T_Flip_Flop t_ff_1 (.T(and_6_out), .clk(Clk_out), .Q(out_4[2]), .reset(Reset));  // open: Qn, preset
  T_Flip_Flop t_ff_2 (.T(and_7_out), .clk(Clk_out), .Q(out_5[0]), .reset(Reset));  // open: Qn, preset
  and and_1 (and_1_out, and_7_out, out_5[0]);
  T_Flip_Flop t_ff_3 (.T(and_4_out), .clk(Clk_out), .Q(out_4[1]), .reset(Reset));  // open: Qn, preset
  T_Flip_Flop t_ff_4 (.T(and_1_out), .clk(Clk_out), .Q(out_5[1]), .reset(Reset));  // open: Qn, preset
  T_Flip_Flop t_ff_5 (.T(not_1_out), .clk(Clk_out), .Q(out_4[0]), .reset(Reset));  // open: Qn, preset
  and and_2 (and_2_out, out_5[0], and_7_out, out_5[1]);
  T_Flip_Flop t_ff_6 (.T(and_2_out), .clk(Clk_out), .Q(out_5[2]), .reset(Reset));  // open: Qn, preset
  T_Flip_Flop t_ff_7 (.T(and_5_out), .clk(Clk_out), .Q(out_5[3]), .reset(Reset));  // open: Qn, preset
  and and_3 (and_3_out, out_4[1], out_4[0]);
  and and_4 (and_4_out, not_1_out, out_4[0]);
  and and_5 (and_5_out, and_2_out, and_7_out, out_5[2]);
  and and_6 (and_6_out, not_1_out, and_3_out);
  and and_7 (and_7_out, and_4_out, out_4[1]);
  Hex_Digit_Display hex_digit_display_1 (.value({in_3, out_4[2:0]}));  // open: dp
  Hex_Digit_Display hex_digit_display_2 (.value(out_5));  // open: dp

  assign out_4[3] = in_3;

  // Notes on the sheet:
  //   Input x
endmodule
