// Logisim project Hardware_Synch.circ as structural Verilog: 1 circuit, main circuit main
module main (
  input  in_1,
  input  Set1,
  input  Set2,
  input  in_4,
  input  Reset1,
  input  Reset2
);

  wire and_1_out, and_2_out, Clk_out, not_1_out, not_2_out, x_out;
  wire [1:0] t_ff_1_q, t_ff_4_q;

  Clock Clk (.out(Clk_out));
  T_Flip_Flop t_ff_1 (.T(in_4), .clk(Clk_out), .Q(t_ff_1_q[0]), .reset(Reset1), .preset(Set1));  // open: Qn
  and and_1 (and_1_out, t_ff_1_q[0], t_ff_1_q[0]);
  T_Flip_Flop t_ff_2 (.T(and_1_out), .clk(Clk_out), .Q(t_ff_1_q[1]), .reset(Reset1), .preset(Set1));  // open: Qn
  not not_1 (not_1_out, t_ff_1_q[0]);
  not not_2 (not_2_out, t_ff_1_q[1]);
  Hex_Digit_Display hex_digit_display_1 (.value({{2{in_1}}, t_ff_1_q}));  // open: dp
  and x (x_out, not_1_out, not_2_out);
  and and_2 (and_2_out, t_ff_4_q[0], x_out);
  T_Flip_Flop t_ff_3 (.T(and_2_out), .clk(Clk_out), .Q(t_ff_4_q[1]), .reset(Reset2), .preset(Set2));  // open: Qn
  T_Flip_Flop t_ff_4 (.T(x_out), .clk(Clk_out), .Q(t_ff_4_q[0]), .reset(Reset2), .preset(Set2));  // open: Qn
  Hex_Digit_Display hex_digit_display_2 (.value({{2{in_1}}, t_ff_4_q}));  // open: dp
endmodule
