// Logisim project Q3.circ as structural Verilog: 1 circuit, main circuit main
module main (
  input  in_1,
  input  in_2,
  input  in_3,
  input  in_4,
  input  in_5
);

  wire and_1_out, and_2_out, and_3_out, clock_1_out, not_1_out, not_2_out, not_3_out;
  wire [0:0] and_4_out;
  wire [2:0] t_ff_1_q;
  wire [3:0] adder_1_out, d_ff_4_q, t_ff_3_q;

  Clock clock_1 (.out(clock_1_out));
  T_Flip_Flop t_ff_1 (.T(in_4), .clk(clock_1_out), .Q(t_ff_1_q[0]));  // open: Qn, reset, preset
  T_Flip_Flop t_ff_2 (.T(t_ff_1_q[0]), .clk(clock_1_out), .Q(t_ff_1_q[1]));  // open: Qn, reset, preset
  T_Flip_Flop t_ff_3 (.T(in_5), .clk(and_4_out[0]), .Q(t_ff_3_q[0]));  // open: Qn, reset, preset
  and and_1 (and_1_out, t_ff_3_q[0], t_ff_3_q[1]);
  T_Flip_Flop t_ff_4 (.T(t_ff_3_q[0]), .clk(and_4_out[0]), .Q(t_ff_3_q[1]));  // open: Qn, reset, preset
  and and_2 (and_2_out, t_ff_1_q[0], t_ff_1_q[1]);
  T_Flip_Flop t_ff_5 (.T(and_2_out), .clk(clock_1_out), .Q(t_ff_1_q[2]));  // open: Qn, reset, preset
  not not_1 (not_1_out, t_ff_1_q[1]);
  T_Flip_Flop t_ff_6 (.T(and_1_out), .clk(and_4_out[0]), .Q(t_ff_3_q[2]));  // open: Qn, reset, preset
  not not_2 (not_2_out, t_ff_1_q[2]);
  not not_3 (not_3_out, t_ff_1_q[0]);
  Hex_Digit_Display hex_digit_display_1 (.value({in_3, t_ff_1_q}));  // open: dp
  and and_3 (and_3_out, and_1_out, t_ff_3_q[2]);
  T_Flip_Flop t_ff_7 (.T(and_3_out), .clk(and_4_out[0]), .Q(t_ff_3_q[3]));  // open: Qn, reset, preset
  and and_4 (and_4_out[0], not_2_out, not_1_out, not_3_out);
  Hex_Digit_Display hex_digit_display_2 (.value(t_ff_3_q));  // open: dp
  Adder #(.width(4)) adder_1 (
    .a({{3{in_2}}, and_4_out[0]}), .b(d_ff_4_q), .out(adder_1_out), .cin(in_1));  // open: cout
  D_Flip_Flop d_ff_1 (.D(adder_1_out[3]), .clk(clock_1_out), .Q(d_ff_4_q[3]));  // open: Qn, preset, reset
  D_Flip_Flop d_ff_2 (.D(adder_1_out[2]), .clk(clock_1_out), .Q(d_ff_4_q[2]));  // open: Qn, preset, reset
  D_Flip_Flop d_ff_3 (.D(adder_1_out[1]), .clk(clock_1_out), .Q(d_ff_4_q[1]));  // open: Qn, preset, reset
  D_Flip_Flop d_ff_4 (.D(adder_1_out[0]), .clk(clock_1_out), .Q(d_ff_4_q[0]));  // open: Qn, preset, reset
  Hex_Digit_Display hex_digit_display_3 (.value(adder_1_out));  // open: dp
endmodule
