// Logisim project B2G.circ as structural Verilog: 1 circuit, main circuit main
module main (
  input  [3:0] in_1
);

  wire [2:0] B0x1_out;

  xor B0x1 (B0x1_out[0], in_1[0], in_1[1]);
  xor B1x2 (B0x1_out[1], in_1[1], in_1[2]);
  xor B2x3 (B0x1_out[2], in_1[2], in_1[3]);
  Hex_Digit_Display hex_digit_display_1 (.value({in_1[3], B0x1_out}));  // open: dp
endmodule
