// Logisim project G2B.circ as structural Verilog: 1 circuit, main circuit main
module main (
  input  [3:0] in_1
);

  wire [2:0] G3x2x1x0_out;

  xor G3x2 (G3x2x1x0_out[2], in_1[2], in_1[3]);
  xor G3x2x1 (G3x2x1x0_out[1], in_1[1], G3x2x1x0_out[2]);
  xor G3x2x1x0 (G3x2x1x0_out[0], in_1[0], G3x2x1x0_out[1]);
  Hex_Digit_Display hex_digit_display_1 (.value({in_1[3], G3x2x1x0_out}));  // open: dp
endmodule
