// Logisim project FA_and_FSFA.circ as structural Verilog: 1 circuit, main circuit main
module main (
  input  in_1,
  input  [3:0] in_2,
  input  [3:0] in_3,
  input  in_4,
  input  in_5,
  input  in_6,
  output C4,
  output out_8,
  output out_9,
  output out_10,
  output out_11
);

  wire and_1_out, and_2_out, and_3_out, and_4_out, and_5_out, and_6_out, and_7_out, and_8_out, or_1_out,
       or_2_out, or_3_out, xor_1_out, xor_2_out, xor_3_out, xor_4_out, xor_5_out, xor_6_out, xor_7_out,
       xor_8_out;
  wire [0:0] xor_13_out;

  xor xor_1 (xor_1_out, in_3[0], in_1);
  xor xor_2 (xor_2_out, in_3[1], in_1);
  xor xor_3 (xor_3_out, in_3[2], in_1);
  xor xor_4 (xor_4_out, in_3[3], in_1);
  xor xor_5 (xor_5_out, xor_1_out, in_2[0]);
  and and_1 (and_1_out, xor_1_out, in_2[0]);
  xor xor_6 (xor_6_out, xor_2_out, in_2[1]);
  and and_2 (and_2_out, xor_2_out, in_2[1]);
  xor xor_7 (xor_7_out, xor_3_out, in_2[2]);
  and and_3 (and_3_out, xor_3_out, in_2[2]);
  xor xor_8 (xor_8_out, xor_4_out, in_2[3]);
  and and_4 (and_4_out, xor_4_out, in_2[3]);
  xor xor_9 (out_11, xor_5_out, in_1);
  and and_5 (and_5_out, xor_5_out, in_1);
  xor xor_10 (out_10, xor_6_out, or_1_out);
  and and_6 (and_6_out, xor_6_out, or_1_out);
  xor xor_11 (out_9, xor_7_out, or_2_out);
  and and_7 (and_7_out, xor_7_out, or_2_out);
  xor xor_12 (out_8, xor_8_out, or_3_out);
  and and_8 (and_8_out, xor_8_out, or_3_out);
  or or_1 (or_1_out, and_5_out, and_1_out);
  or or_2 (or_2_out, and_6_out, and_2_out);
  or or_3 (or_3_out, and_7_out, and_3_out);
  or or_4 (C4, and_8_out, and_4_out);
  xor xor_13 (xor_13_out[0], C4, in_1);
  Hex_Digit_Display hex_digit_display_1 (.value({{2{in_5}}, in_4, xor_13_out[0]}));  // open: dp
  Hex_Digit_Display hex_digit_display_2 (.value({out_8, out_9, out_10, out_11}));  // open: dp

  assign in_6 = in_5;

  // Notes on the sheet:
  //   C0
  //   Y
  //   X
  //   C1
  //   C2
  //   C3
  //   S3
  //   S1
  //   S2
  //   S0
endmodule
