// Logisim project BCD_Adder.circ as structural Verilog: 3 circuits, main circuit main
module main (
  input  x3,
  input  x2,
  input  x1,
  input  x0,
  input  in_5,
  input  in_6,
  input  y3,
  input  y2,
  input  y1,
  input  y0,
  output b0,
  output b1,
  output b2,
  output b3,
  output b4
);

  wire and_1_out, and_2_out, fullbitadder_1_s0, fullbitadder_1_s1, fullbitadder_1_s2, fullbitadder_1_s3;

  Fullbitadder fullbitadder_1 (
    .C(in_5), .X0(x0), .Y0(y0), .X1(x1), .Y1(y1), .X2(x2), .Y2(y2), .X3(x3), .Y3(y3), .S0(fullbitadder_1_s0),
    .S1(fullbitadder_1_s1), .S2(fullbitadder_1_s2), .S3(fullbitadder_1_s3));  // open: Cout
  and and_1 (and_1_out, fullbitadder_1_s1, fullbitadder_1_s3);
  or or_1 (b4, and_1_out, and_2_out);
  and and_2 (and_2_out, fullbitadder_1_s2, fullbitadder_1_s3);
  Fullbitadder fullbitadder_2 (
    .C(in_5), .X0(fullbitadder_1_s0), .Y0(in_6), .X1(fullbitadder_1_s1), .Y1(b4), .X2(fullbitadder_1_s2),
    .Y2(b4), .X3(fullbitadder_1_s1), .Y3(in_6), .S0(b0), .S1(b1), .S2(b2), .S3(b3));  // open: Cout
endmodule

module Fullbitadder (
  input  C,
  input  X0,
  input  Y0,
  input  X1,
  input  Y1,
  input  X2,
  input  Y2,
  input  X3,
  input  Y3,
  output S0,
  output S1,
  output S2,
  output S3,
  output Cout
);

  wire fulladder_1_carry, fulladder_2_carry, fulladder_3_carry;

  fulladder fulladder_1 (.X(X0), .Z(Y0), .Y(C), .Sum(S0), .Carry(fulladder_1_carry));
  fulladder fulladder_2 (.X(X1), .Z(Y1), .Y(fulladder_1_carry), .Sum(S1), .Carry(fulladder_2_carry));
  fulladder fulladder_3 (.X(X2), .Z(Y2), .Y(fulladder_2_carry), .Sum(S2), .Carry(fulladder_3_carry));
  fulladder fulladder_4 (.X(X3), .Z(Y3), .Y(fulladder_3_carry), .Sum(S3), .Carry(Cout));
endmodule

module fulladder (
  input  X,
  input  Z,
  input  Y,
  output Sum,
  output Carry
);

  wire and_1_out, and_2_out, xor_1_out;

  xor xor_1 (xor_1_out, X, Y);
  and and_1 (and_1_out, X, Y);
  xor xor_2 (Sum, xor_1_out, Z);
  and and_2 (and_2_out, Z, xor_1_out);
  or or_1 (Carry, and_1_out, and_2_out);
endmodule
