// Logisim project bcd.circ as structural Verilog: 1 circuit, main circuit main
module main (
  input  in_1,
  input  in_2,
  input  in_3,
  input  [3:0] in_4,
  output b3,
  output b2,
  output b1,
  output b0
);

  wire and_1_out, and_2_out, and_4_out, and_5_out, and_6_out, and_7_out, not_1_out, not_2_out, not_3_out;
  wire [3:3] or_1_out;

  not not_1 (not_1_out, in_4[1]);
  not not_2 (not_2_out, in_4[2]);
  and and_1 (and_1_out, in_4[0], in_4[2]);
  and and_2 (and_2_out, in_4[0], in_4[1]);
  and and_3 (b3, in_4[0], not_2_out);
  and and_4 (and_4_out, in_4[2], in_4[1]);
  and and_5 (and_5_out, in_4[1], not_3_out);
  not not_3 (not_3_out, in_4[0]);
  and and_6 (and_6_out, not_3_out, in_4[2]);
  and and_7 (and_7_out, in_4[0], in_4[1], in_4[2]);
  or or_1 (or_1_out[3], and_1_out, and_2_out);
  or or_2 (b2, and_4_out, and_5_out);
  or or_3 (b1, and_6_out, and_7_out);
  Hex_Digit_Display hex_digit_display_1 (.value({or_1_out[3], in_3, in_2, in_1}));  // open: dp
  Hex_Digit_Display hex_digit_display_2 (.value({b3, b2, b1, in_4[3]}));  // open: dp

  assign b0 = in_4[3];
endmodule
