// Logisim project 3-8 decoder.circ as structural Verilog
module DECODE (
  input  A,
  input  B,
  input  C,
  output A1,
  output A2,
  output A3,
  output A4,
  output A5,
  output A6,
  output A7,
  output A8
);

  wire not_1_out, not_2_out, not_3_out;

  not not_1 (not_1_out, A);
  not not_2 (not_2_out, B);
  not not_3 (not_3_out, C);
  and and_1 (A1, not_1_out, not_2_out, not_3_out);
  and and_2 (A2, not_1_out, not_2_out, C);
  and and_3 (A3, not_1_out, B, not_3_out);
  and and_4 (A4, not_1_out, B, C);
  and and_5 (A5, A, not_2_out, not_3_out);
  and and_6 (A6, A, not_2_out, C);
  and and_7 (A7, A, B, not_3_out);
  and and_8 (A8, A, B, C);
endmodule

module MULTIPLEX (
  input  S1,
  input  S2,
  input  S3,
  input  S4,
  input  S5,
  input  S6,
  input  S7,
  input  S8,
  input  in_9,
  input  in_10,
  input  in_11,
  output OU
);

  wire and_1_out, and_2_out, and_3_out, and_4_out, and_5_out, and_6_out, and_7_out, and_8_out, decode_1_a1,
       decode_1_a2, decode_1_a3, decode_1_a4, decode_1_a5, decode_1_a6, decode_1_a7, decode_1_a8;

  DECODE decode_1 (
    .A(in_9), .B(in_10), .C(in_11), .A1(decode_1_a1), .A2(decode_1_a2), .A3(decode_1_a3), .A4(decode_1_a4),
    .A5(decode_1_a5), .A6(decode_1_a6), .A7(decode_1_a7), .A8(decode_1_a8));
  and and_1 (and_1_out, S1, decode_1_a1);
  and and_2 (and_2_out, S2, decode_1_a2);
  and and_3 (and_3_out, S3, decode_1_a3);
  and and_4 (and_4_out, S4, decode_1_a4);
  and and_5 (and_5_out, S5, decode_1_a5);
  and and_6 (and_6_out, S6, decode_1_a6);
  and and_7 (and_7_out, S7, decode_1_a7);
  and and_8 (and_8_out, S8, decode_1_a8);
  or or_1 (OU, and_1_out, and_2_out, and_3_out, and_4_out, and_5_out, and_6_out, and_7_out, and_8_out);
endmodule
