// Logisim project Q_2.circ as structural Verilog: 1 circuit, main circuit main
module main (
  input  in_1,
  input  in_2,
  input  in_3,
  output [2:0] out_4,
  output [3:0] out_5
);

  wire and_1_out, and_2_out, and_3_out, and_4_out, and_5_out, and_6_out, clock_1_out, clock_2_out,
       j_k_ff_1_qn, j_k_ff_3_qn, not_1_out, not_2_out, not_3_out, or_1_out;

  not not_1 (not_1_out, out_4[2]);
  not not_2 (not_2_out, out_4[1]);
  not not_3 (not_3_out, out_4[0]);
  and and_1 (and_1_out, not_1_out, not_2_out, not_3_out);
  and and_2 (and_2_out, out_4[2], not_2_out, not_3_out);
  or or_1 (or_1_out, and_1_out, and_2_out);
  J_K_Flip_Flop #(.trigger("falling")) j_k_ff_1 (
    .J(in_1), .K(in_1), .clk(clock_1_out), .Q(out_4[0]), .Qn(j_k_ff_1_qn), .reset(in_2));  // open: preset
  Clock clock_1 (.out(clock_1_out));
  J_K_Flip_Flop #(.trigger("falling")) j_k_ff_2 (
    .J(or_1_out), .K(or_1_out), .clk(clock_2_out), .Q(out_5[0]), .reset(in_3));  // open: Qn, preset
  Clock clock_2 (.out(clock_2_out));
  and and_3 (and_3_out, or_1_out, out_5[0]);
  J_K_Flip_Flop #(.trigger("falling")) j_k_ff_3 (
    .J(j_k_ff_1_qn), .K(j_k_ff_1_qn), .clk(clock_1_out), .Q(out_4[1]), .Qn(j_k_ff_3_qn), .reset(in_2));  // open: preset
  J_K_Flip_Flop #(.trigger("falling")) j_k_ff_4 (
    .J(and_3_out), .K(and_3_out), .clk(clock_2_out), .Q(out_5[1]), .reset(in_3));  // open: Qn, preset
  and and_4 (and_4_out, j_k_ff_1_qn, j_k_ff_3_qn);
  J_K_Flip_Flop #(.trigger("falling")) j_k_ff_5 (
    .J(and_4_out), .K(and_4_out), .clk(clock_1_out), .Q(out_4[2]), .reset(in_2));  // open: Qn, preset
  and and_5 (and_5_out, and_3_out, out_5[1]);
  J_K_Flip_Flop #(.trigger("falling")) j_k_ff_6 (
    .J(and_5_out), .K(and_5_out), .clk(clock_2_out), .Q(out_5[2]), .reset(in_3));  // open: Qn, preset
  and and_6 (and_6_out, and_5_out, out_5[2]);
  J_K_Flip_Flop #(.trigger("falling")) j_k_ff_7 (
    .J(and_6_out), .K(and_6_out), .clk(clock_2_out), .Q(out_5[3]), .reset(in_3));  // open: Qn, preset
endmodule
