// Logisim project Q_3.circ as structural Verilog
module main (
  input  in_1,
  input  in_2,
  input  in_3,
  input  in_4,
  input  in_5
);

  wire and_1_out, and_2_out, and_3_out, button_1_out, button_2_out, clock_1_out, j_k_ff_1_qn, j_k_ff_2_qn,
       not_1_out, or_1_out;
  wire [0:0] multiplexer_1_out;
  wire [2:0] j_k_ff_1_q;
  wire [3:0] d_ff_1_q;
  wire [7:0] adder_1_out;

  Button #(.press("passive")) button_1 (.out(button_1_out));
  Multiplexer multiplexer_1 (.in0(in_5), .in1(button_1_out), .out(multiplexer_1_out[0]), .sel(or_1_out));
  or or_1 (or_1_out, and_1_out, and_2_out);
  and and_1 (and_1_out, j_k_ff_1_q[0], j_k_ff_1_q[1], j_k_ff_1_q[2]);
  Adder adder_1 (
    .a({{4{in_3}}, d_ff_1_q}), .b({{7{in_3}}, multiplexer_1_out[0]}), .out(adder_1_out), .cin(in_4));  // open: cout
  Button #(.press("passive")) button_2 (.out(button_2_out));
  J_K_Flip_Flop #(.trigger("falling")) j_k_ff_1 (
    .J(button_2_out), .K(button_2_out), .clk(clock_1_out), .Q(j_k_ff_1_q[0]), .Qn(j_k_ff_1_qn), .reset(in_1));  // open: preset
  Clock clock_1 (.out(clock_1_out));
  and and_2 (and_2_out, not_1_out, j_k_ff_1_q[1], j_k_ff_1_q[2]);
  D_Flip_Flop d_ff_1 (.D(adder_1_out[0]), .clk(or_1_out), .Q(d_ff_1_q[0]));  // open: Qn, preset, reset
  not not_1 (not_1_out, j_k_ff_1_q[0]);
  D_Flip_Flop d_ff_2 (.D(adder_1_out[1]), .clk(or_1_out), .Q(d_ff_1_q[1]));  // open: Qn, preset, reset
  J_K_Flip_Flop #(.trigger("falling")) j_k_ff_2 (
    .J(j_k_ff_1_qn), .K(j_k_ff_1_qn), .clk(clock_1_out), .Q(j_k_ff_1_q[1]), .Qn(j_k_ff_2_qn), .reset(in_1));  // open: preset
  D_Flip_Flop d_ff_3 (.D(adder_1_out[2]), .clk(or_1_out), .Q(d_ff_1_q[2]));  // open: Qn, preset, reset
  and and_3 (and_3_out, j_k_ff_1_qn, j_k_ff_2_qn);
  J_K_Flip_Flop #(.trigger("falling")) j_k_ff_3 (
    .J(and_3_out), .K(and_3_out), .clk(clock_1_out), .Q(j_k_ff_1_q[2]), .reset(in_1));  // open: Qn, preset
  D_Flip_Flop d_ff_4 (.D(adder_1_out[3]), .clk(or_1_out), .Q(d_ff_1_q[3]));  // open: Qn, preset, reset
  Hex_Digit_Display hex_digit_display_1 (.value({in_2, j_k_ff_1_q}));  // open: dp
  Hex_Digit_Display hex_digit_display_2 (.value(d_ff_1_q));  // open: dp
endmodule
