// Logisim project EndSemQ1 (Not Working).circ as structural Verilog: 5 circuits, main circuit main
module main (
  input  [1:0] in_1,
  input  Set,
  input  in_3,
  input  Reset
);

  wire clock_1_out, dc_1_d0, dc_1_d1, dc_1_d2, dc_1_d3, e3_1_e0, e3_1_e1, e3_1_e2, e3_1_e33,
       multiplexer_1_out, multiplexer_2_out, multiplexer_3_out, multiplexer_4_out, r_1_d0, r_1_d1, r_1_d2,
       r_1_d3, rc_1_d0, rc_1_d1, rc_1_d2, rc_1_d3;
  wire [3:0] d_ff_4_q;

  Clock clock_1 (.out(clock_1_out));
  Multiplexer #(.select(2)) multiplexer_1 (
    .in0(dc_1_d3), .in1(e3_1_e33), .in2(rc_1_d3), .in3(r_1_d3), .out(multiplexer_1_out), .sel(in_1));
  D_Flip_Flop d_ff_1 (
    .D(multiplexer_1_out), .clk(clock_1_out), .Q(d_ff_4_q[3]), .preset(in_3), .reset(Reset));  // open: Qn
  Multiplexer #(.select(2)) multiplexer_2 (
    .in0(dc_1_d2), .in1(e3_1_e2), .in2(rc_1_d2), .in3(r_1_d2), .out(multiplexer_2_out), .sel(in_1));
  D_Flip_Flop d_ff_2 (
    .D(multiplexer_2_out), .clk(clock_1_out), .Q(d_ff_4_q[2]), .preset(Set), .reset(Reset));  // open: Qn
  Multiplexer #(.select(2)) multiplexer_3 (
    .in0(dc_1_d1), .in1(e3_1_e1), .in2(rc_1_d1), .in3(r_1_d1), .out(multiplexer_3_out), .sel(in_1));
  D_Flip_Flop d_ff_3 (
    .D(multiplexer_3_out), .clk(clock_1_out), .Q(d_ff_4_q[1]), .preset(Set), .reset(Reset));  // open: Qn
  Hex_Digit_Display hex_digit_display_1 (.value(d_ff_4_q));  // open: dp
  D_Flip_Flop d_ff_4 (
    .D(multiplexer_4_out), .clk(clock_1_out), .Q(d_ff_4_q[0]), .preset(Set), .reset(Reset));  // open: Qn
  Multiplexer #(.select(2)) multiplexer_4 (
    .in0(dc_1_d0), .in1(e3_1_e0), .in2(rc_1_d0), .in3(r_1_d0), .out(multiplexer_4_out), .sel(in_1));
  DC dc_1 (
    .Q0(d_ff_4_q[0]), .Q1(d_ff_4_q[1]), .Q2(d_ff_4_q[2]), .Q3(d_ff_4_q[3]), .D0(dc_1_d0), .D3(dc_1_d3),
    .D2(dc_1_d2), .D1(dc_1_d1));
  E3 e3_1 (
    .B0(dc_1_d0), .B1(dc_1_d1), .B2(dc_1_d2), .B3(dc_1_d3), .E0(e3_1_e0), .E1(e3_1_e1), .E2(e3_1_e2),
    .E33(e3_1_e33));
  RC rc_1 (
    .Q0(d_ff_4_q[0]), .Q1(d_ff_4_q[1]), .Q2(d_ff_4_q[2]), .Q3(d_ff_4_q[3]), .D0(rc_1_d0), .D1(rc_1_d1),
    .D2(rc_1_d2), .D3(rc_1_d3));
  R r_1 (
    .Q0(d_ff_4_q[0]), .Q1(d_ff_4_q[1]), .Q2(d_ff_4_q[2]), .Q3(d_ff_4_q[3]), .D0(r_1_d0), .D1(r_1_d1),
    .D2(r_1_d2), .D3(r_1_d3));
endmodule

module DC (
  input  Q0,
  input  Q1,
  input  Q2,
  input  Q3,
  output D0,
  output D3,
  output D2,
  output D1
);

  wire and_1_out, and_2_out, and_3_out, and_4_out, not_1_out, not_2_out, not_4_out, or_1_out, or_2_out,
       xor_1_out;

  not not_1 (not_1_out, Q2);
  not not_2 (not_2_out, Q3);
  not not_3 (D0, Q0);
  not not_4 (not_4_out, Q1);
  or or_1 (or_1_out, D0, not_4_out);
  xor xor_1 (xor_1_out, Q0, Q1);
  or or_2 (or_2_out, not_1_out, or_1_out);
  and and_1 (and_1_out, not_1_out, or_1_out);
  and and_2 (and_2_out, Q0, Q1, Q2);
  not not_5 (D1, xor_1_out);
  and and_3 (and_3_out, or_2_out, not_2_out);
  and and_4 (and_4_out, Q0, Q1, Q2, Q3);
  or or_3 (D2, and_1_out, and_2_out);
  or or_4 (D3, and_3_out, and_4_out);
endmodule

module E3 (
  input  B0,
  input  B1,
  input  B2,
  input  B3,
  output E0,
  output E1,
  output E2,
  output E33
);

  wire and_1_out, and_2_out, and_3_out, and_4_out, and_5_out, not_1_out, not_2_out, xor_1_out;

  not not_1 (not_1_out, B1);
  not not_2 (not_2_out, B2);
  not not_3 (E0, B0);
  xor xor_1 (xor_1_out, B0, B1);
  and and_1 (and_1_out, E0, not_1_out, B2);
  not not_4 (E1, xor_1_out);
  and and_2 (and_2_out, B1, not_2_out);
  and and_3 (and_3_out, B0, not_2_out);
  and and_4 (and_4_out, B2, B0);
  and and_5 (and_5_out, B2, B1);
  or or_1 (E2, and_2_out, and_1_out, and_3_out);
  or or_2 (E33, and_4_out, B3, and_5_out);
endmodule

module RC (
  input  Q0,
  input  Q1,
  input  Q2,
  input  Q3,
  output D0,
  output D1,
  output D2,
  output D3
);


  assign D0 = Q1;
  assign D1 = Q2;
  assign D2 = Q3;
  assign D3 = Q0;
endmodule

module R (
  input  Q0,
  input  Q1,
  input  Q2,
  input  Q3,
  output D0,
  output D1,
  output D2,
  output D3
);


  assign D0 = Q0;
  assign D1 = Q1;
  assign D2 = Q2;
  assign D3 = Q3;
endmodule
