// Logisim project Software_EndSemQ1 (Incomplete).circ as structural Verilog: 2 circuits, main circuit main
module main (
  input  [1:0] in_1,
  input  in_2,
  input  in_3,
  input  in_4,
  input  in_5
);

  wire and_1_out, and_2_out, and_3_out, and_4_out, and_5_out, and_6_out, and_7_out, and_8_out, and_9_out,
       clock_1_out, d_ff_2_qn, d_ff_3_qn, d_ff_4_qn, excess3_1_s0, excess3_1_s1, excess3_1_s2, excess3_1_s3,
       multiplexer_1_out, multiplexer_2_out, multiplexer_3_out, multiplexer_4_out, not_1_out, not_2_out,
       not_3_out, not_4_out, or_1_out, or_2_out, or_3_out, xnor_1_out;
  wire [3:0] d_ff_4_q;

  not not_1 (not_1_out, d_ff_4_q[3]);
  not not_2 (not_2_out, d_ff_4_q[2]);
  not not_3 (not_3_out, d_ff_4_q[1]);
  not not_4 (not_4_out, d_ff_4_q[0]);
  and and_1 (and_1_out, d_ff_4_q[3], d_ff_4_q[2]);
  and and_2 (and_2_out, d_ff_4_q[3], d_ff_4_q[1]);
  and and_3 (and_3_out, d_ff_4_q[3], d_ff_4_q[0]);
  and and_4 (and_4_out, not_1_out, not_2_out, not_3_out, not_4_out);
  Clock clock_1 (.out(clock_1_out));
  or or_1 (or_1_out, and_1_out, and_2_out, and_3_out, and_4_out);
  Multiplexer #(.select(2)) multiplexer_1 (
    .in0(or_1_out), .in1(d_ff_4_q[0]), .in2(excess3_1_s3), .in3(d_ff_4_q[3]), .out(multiplexer_1_out),
    .sel(in_1));
  D_Flip_Flop d_ff_1 (.D(multiplexer_1_out), .clk(clock_1_out), .Q(d_ff_4_q[3]), .preset(in_4));  // open: Qn, reset
  and and_5 (and_5_out, d_ff_4_q[2], d_ff_4_q[1]);
  and and_6 (and_6_out, d_ff_4_q[2], d_ff_4_q[0]);
  and and_7 (and_7_out, d_ff_2_qn, d_ff_3_qn, d_ff_4_qn);
  Multiplexer #(.select(2)) multiplexer_2 (
    .in0(or_2_out), .in1(d_ff_4_q[3]), .in2(excess3_1_s2), .in3(d_ff_4_q[2]), .out(multiplexer_2_out),
    .sel(in_1));
  D_Flip_Flop d_ff_2 (
    .D(multiplexer_2_out), .clk(clock_1_out), .Q(d_ff_4_q[2]), .Qn(d_ff_2_qn), .reset(in_5));  // open: preset
  or or_2 (or_2_out, and_5_out, and_6_out, and_7_out);
  xnor xnor_1 (xnor_1_out, d_ff_4_q[0], d_ff_4_q[1]);
  Multiplexer #(.select(2)) multiplexer_3 (
    .in0(xnor_1_out), .in1(d_ff_4_q[2]), .in2(excess3_1_s1), .in3(d_ff_4_q[1]), .out(multiplexer_3_out),
    .sel(in_1));
  D_Flip_Flop d_ff_3 (
    .D(multiplexer_3_out), .clk(clock_1_out), .Q(d_ff_4_q[1]), .Qn(d_ff_3_qn), .reset(in_5));  // open: preset
  D_Flip_Flop d_ff_4 (
    .D(multiplexer_4_out), .clk(clock_1_out), .Q(d_ff_4_q[0]), .Qn(d_ff_4_qn), .reset(in_5));  // open: preset
  and and_8 (and_8_out, d_ff_4_qn, d_ff_4_q[1]);
  or or_3 (or_3_out, and_8_out, and_9_out);
  and and_9 (and_9_out, d_ff_4_qn, d_ff_3_qn);
  Multiplexer #(.select(2)) multiplexer_4 (
    .in0(or_3_out), .in1(d_ff_4_q[1]), .in2(excess3_1_s0), .in3(d_ff_4_q[0]), .out(multiplexer_4_out),
    .sel(in_1));
  Hex_Digit_Display hex_digit_display_1 (.value(d_ff_4_q));  // open: dp
  Excess3 excess3_1 (
    .GND(in_2), .VCC(in_3), .A3(d_ff_4_q[3]), .A2(d_ff_4_q[2]), .A1(d_ff_4_q[1]), .A0(d_ff_4_q[0]),
    .S3(excess3_1_s3), .S2(excess3_1_s2), .S1(excess3_1_s1), .S0(excess3_1_s0));
endmodule

module Excess3 (
  input  GND,
  input  VCC,
  input  A3,
  input  A2,
  input  A1,
  input  A0,
  output S3,
  output S2,
  output S1,
  output S0
);

  _74283 u_74283_1 (
    .pin1(S1), .pin2(VCC), .pin3(A1), .pin4(S0), .pin5(A0), .pin6(VCC), .pin7(GND), .pin15(GND), .pin14(A2),
    .pin13(S2), .pin12(A3), .pin11(GND), .pin10(S3));  // open: pin9
endmodule
