// Logisim project Q2.circ as structural Verilog: 1 circuit, main circuit main
module main (
  input  A,
  input  B,
  input  C
);

  wire AB_out, AC_out, ApB_out, ApBCp_out, BC_out, not_1_out, not_2_out, or_1_out, or_2_out, or_3_out;

  not not_1 (not_1_out, A);
  not not_2 (not_2_out, C);
  and AC (AC_out, A, C);
  and AB (AB_out, A, B);
  and BC (BC_out, B, C);
  and ApB (ApB_out, B, not_1_out);
  or or_1 (or_1_out, AC_out, AB_out);
  or or_2 (or_2_out, or_1_out, BC_out);
  and ApBCp (ApBCp_out, ApB_out, not_2_out);
  or or_3 (or_3_out, or_2_out, ApBCp_out);
  LED led_1 (.in(or_3_out));
endmodule
