// Logisim project Q4.circ as structural Verilog: 1 circuit, main circuit main
module main (
  input  A,
  input  B,
  input  C,
  input  D,
  output out_5
);

  wire ABC_out, ABCDp_out, ABpCD_out, AC_out, ACD_out, AD_out, BCD_out, CD_out, not_1_out, not_2_out,
       or_1_out, or_2_out, or_3_out;

  not not_1 (not_1_out, B);
  not not_2 (not_2_out, D);
  and AC (AC_out, A, C);
  and CD (CD_out, C, D);
  and AD (AD_out, A, D);
  and ABC (ABC_out, AC_out, B);
  and BCD (BCD_out, B, CD_out);
  and ACD (ACD_out, C, AD_out);
  and ABCDp (ABCDp_out, ABC_out, not_2_out);
  and ABpCD (ABpCD_out, not_1_out, ACD_out);
  or or_1 (or_1_out, ABC_out, BCD_out);
  or or_2 (or_2_out, ABCDp_out, ABpCD_out);
  or or_3 (or_3_out, or_1_out, or_2_out);
  or or_4 (out_5, or_3_out, ACD_out);
endmodule
