// Logisim project Q3.circ as structural Verilog: 1 circuit, main circuit main
module main (
  input  A,
  input  B,
  input  C,
  input  D
);

  wire AC_out, AcD_out, ACDc_out, BcDc_out, F_out, not_1_out, not_2_out, not_3_out, or_1_out;

  not not_1 (not_1_out, A);
  not not_2 (not_2_out, B);
  not not_3 (not_3_out, D);
  and AcD (AcD_out, not_1_out, D);
  and BcDc (BcDc_out, not_2_out, not_3_out);
  and AC (AC_out, A, C);
  and ACDc (ACDc_out, AC_out, not_3_out);
  or or_1 (or_1_out, AcD_out, BcDc_out);
  or F (F_out, or_1_out, ACDc_out);
  LED led_1 (.in(F_out));
endmodule
