// Logisim project FA_and_FSFA.circ as structural Verilog: 1 circuit, main circuit main
module main (
  input  [3:0] in_1,
  input  in_2,
  input  [3:0] in_3,
  input  [3:0] in_4,
  input  in_5,
  input  in_6,
  input  in_7,
  output Carry,
  output C4,
  output out_10,
  output out_11,
  output out_12,
  output out_13,
  output out_14,
  output out_15,
  output out_16,
  output out_17
);

  wire and_1_out, and_2_out, and_3_out, and_4_out, and_5_out, and_6_out, and_7_out, and_8_out, and_9_out,
       and_10_out, and_11_out, and_12_out, and_13_out, and_14_out, and_15_out, and_16_out, and_17_out,
       not_1_out, not_2_out, or_1_out, or_2_out, or_3_out, or_5_out, or_6_out, or_7_out, xor_1_out,
       xor_2_out, xor_3_out, xor_4_out, xor_5_out, xor_6_out, xor_7_out, xor_8_out, xor_13_out, xor_14_out,
       xor_15_out, xor_16_out, xor_17_out, xor_18_out, xor_19_out, xor_20_out;
  wire [0:0] xor_25_out;

  xor xor_1 (xor_1_out, in_4[0], in_2);
  xor xor_2 (xor_2_out, in_4[1], in_2);
  xor xor_3 (xor_3_out, in_4[2], in_2);
  xor xor_4 (xor_4_out, in_4[3], in_2);
  xor xor_5 (xor_5_out, xor_1_out, in_3[0]);
  and and_1 (and_1_out, xor_1_out, in_3[0]);
  xor xor_6 (xor_6_out, xor_2_out, in_3[1]);
  and and_2 (and_2_out, xor_2_out, in_3[1]);
  xor xor_7 (xor_7_out, xor_3_out, in_3[2]);
  and and_3 (and_3_out, xor_3_out, in_3[2]);
  xor xor_8 (xor_8_out, xor_4_out, in_3[3]);
  and and_4 (and_4_out, xor_4_out, in_3[3]);
  xor xor_9 (out_17, xor_5_out, in_2);
  and and_5 (and_5_out, xor_5_out, in_2);
  xor xor_10 (out_16, xor_6_out, or_1_out);
  and and_6 (and_6_out, xor_6_out, or_1_out);
  xor xor_11 (out_15, xor_7_out, or_2_out);
  and and_7 (and_7_out, xor_7_out, or_2_out);
  xor xor_12 (out_14, xor_8_out, or_3_out);
  and and_8 (and_8_out, xor_8_out, or_3_out);
  or or_1 (or_1_out, and_5_out, and_1_out);
  or or_2 (or_2_out, and_6_out, and_2_out);
  or or_3 (or_3_out, and_7_out, and_3_out);
  or or_4 (Carry, and_8_out, and_4_out);
  not not_1 (not_1_out, Carry);
  and and_9 (and_9_out, not_1_out, in_2);
  xor xor_13 (xor_13_out, and_9_out, out_17);
  xor xor_14 (xor_14_out, out_16, and_9_out);
  xor xor_15 (xor_15_out, out_15, and_9_out);
  xor xor_16 (xor_16_out, out_14, and_9_out);
  xor xor_17 (xor_17_out, xor_13_out, in_1[0]);
  and and_10 (and_10_out, xor_13_out, in_1[0]);
  xor xor_18 (xor_18_out, xor_14_out, in_1[1]);
  and and_11 (and_11_out, xor_14_out, in_1[1]);
  xor xor_19 (xor_19_out, xor_15_out, in_1[2]);
  and and_12 (and_12_out, xor_15_out, in_1[2]);
  xor xor_20 (xor_20_out, xor_16_out, in_1[3]);
  and and_13 (and_13_out, xor_16_out, in_1[3]);
  xor xor_21 (out_13, xor_17_out, and_9_out);
  and and_14 (and_14_out, xor_17_out, and_9_out);
  xor xor_22 (out_12, xor_18_out, or_5_out);
  and and_15 (and_15_out, xor_18_out, or_5_out);
  xor xor_23 (out_11, xor_19_out, or_6_out);
  and and_16 (and_16_out, xor_19_out, or_6_out);
  xor xor_24 (out_10, xor_20_out, or_7_out);
  and and_17 (and_17_out, xor_20_out, or_7_out);
  or or_5 (or_5_out, and_14_out, and_10_out);
  or or_6 (or_6_out, and_15_out, and_11_out);
  or or_7 (or_7_out, and_16_out, and_12_out);
  or or_8 (C4, and_17_out, and_13_out);
  xor xor_25 (xor_25_out[0], C4, and_9_out);
  LED led_1 (.in(and_9_out));
  Hex_Digit_Display hex_digit_display_1 (.value({{2{in_6}}, in_5, xor_25_out[0]}));  // open: dp
  Hex_Digit_Display hex_digit_display_2 (.value({out_10, out_11, out_12, out_13}));  // open: dp
  // AND_Gate and_18 has open pins: in0=Carry, in1=not_2_out, out=open
  not not_2 (not_2_out, in_2);

  assign in_7 = in_6;

  // Notes on the sheet:
  //   C0
  //   Y
  //   X
  //   C1
  //   C2
  //   C3
  //   C4
  //   S3
  //   S1
  //   S2
  //   S0
  //   C1
  //   C2
  //   C3
  //   S3
  //   S2
  //   S1
  //   S0
endmodule
