// Logisim project FullAdder.circ as structural Verilog: 1 circuit, main circuit main
module main (
  input  in_1,
  input  [3:0] A,
  input  [3:0] in_3,
  input  [3:0] B,
  input  [3:0] in_5
);

  wire and_1_out, and_2_out, and_3_out, and_4_out, and_5_out, and_6_out, and_7_out, and_8_out, and_9_out,
       and_10_out, and_11_out, and_12_out, and_13_out, and_14_out, and_15_out, and_16_out, or_1_out,
       or_2_out, or_3_out, or_4_out, or_5_out, or_6_out, or_7_out, xor_2_out, xor_3_out, xor_4_out,
       xor_8_out, xor_9_out, xor_10_out, xor_11_out, xor_13_out, xor_14_out, xor_15_out;
  wire [3:0] xor_1_out, xor_12_out;

  xor xor_1 (xor_1_out[0], A[0], B[0]);
  and and_1 (and_1_out, A[0], B[0]);
  xor xor_2 (xor_2_out, A[1], B[1]);
  and and_2 (and_2_out, B[1], A[1]);
  xor xor_3 (xor_3_out, A[2], B[2]);
  and and_3 (and_3_out, B[2], A[2]);
  xor xor_4 (xor_4_out, A[3], B[3]);
  and and_4 (and_4_out, B[3], A[3]);
  xor xor_5 (xor_1_out[1], xor_2_out, and_1_out);
  and and_5 (and_5_out, and_1_out, xor_2_out);
  xor xor_6 (xor_1_out[2], xor_3_out, or_1_out);
  and and_6 (and_6_out, or_1_out, xor_3_out);
  xor xor_7 (xor_1_out[3], xor_4_out, or_2_out);
  and and_7 (and_7_out, or_2_out, xor_4_out);
  or or_1 (or_1_out, and_5_out, and_2_out);
  or or_2 (or_2_out, and_6_out, and_3_out);
  or or_3 (or_3_out, and_7_out, and_4_out);
  LED C4 (.in(or_3_out));
  Hex_Digit_Display hex_digit_display_1 (.value(xor_1_out));  // open: dp
  xor xor_8 (xor_8_out, in_1, in_5[0]);
  xor xor_9 (xor_9_out, in_1, in_5[1]);
  xor xor_10 (xor_10_out, in_1, in_5[2]);
  xor xor_11 (xor_11_out, in_1, in_5[3]);
  xor xor_12 (xor_12_out[0], in_3[0], xor_8_out);
  and and_8 (and_8_out, in_3[0], xor_8_out);
  xor xor_13 (xor_13_out, in_3[1], xor_9_out);
  and and_9 (and_9_out, xor_9_out, in_3[1]);
  xor xor_14 (xor_14_out, in_3[2], xor_10_out);
  and and_10 (and_10_out, xor_10_out, in_3[2]);
  xor xor_15 (xor_15_out, in_3[3], xor_11_out);
  and and_11 (and_11_out, xor_11_out, in_3[3]);
  xor xor_16 (xor_12_out[1], xor_13_out, and_8_out);
  and and_12 (and_12_out, and_8_out, xor_13_out);
  xor xor_17 (xor_12_out[2], xor_14_out, or_4_out);
  and and_13 (and_13_out, or_4_out, xor_14_out);
  xor xor_18 (xor_12_out[3], xor_15_out, or_5_out);
  and and_14 (and_14_out, or_5_out, xor_15_out);
  // AND_Gate and_15 has open pins: out=and_15_out
  // AND_Gate and_16 has open pins: out=and_16_out
  or or_4 (or_4_out, and_12_out, and_9_out);
  or or_5 (or_5_out, and_13_out, and_10_out);
  or or_6 (or_6_out, and_14_out, and_11_out);
  LED C (.in(or_6_out));
  or or_7 (or_7_out, and_15_out, and_16_out);
  LED led_1 (.in(or_7_out));
  Hex_Digit_Display hex_digit_display_2 (.value(xor_12_out));  // open: dp
endmodule
