// Logisim project FullAdderSubtracter.circ as structural Verilog: 1 circuit, main circuit main
module main (
  input  Add_Subtract,
  input  [3:0] A,
  input  [3:0] B
);

  wire and_1_out, and_2_out, and_3_out, and_4_out, and_5_out, and_6_out, and_7_out, and_8_out, and_9_out,
       and_10_out, not_1_out, not_2_out, not_3_out, or_1_out, or_2_out, or_3_out, or_4_out, or_5_out,
       xor_1_out, xor_2_out, xor_3_out, xor_4_out;
  wire [3:0] xor_5_out;

  not not_1 (not_1_out, A[3]);
  xor xor_1 (xor_1_out, Add_Subtract, B[0]);
  and and_1 (and_1_out, A[0], B[0]);
  xor xor_2 (xor_2_out, Add_Subtract, B[1]);
  and and_2 (and_2_out, B[1], A[1]);
  xor xor_3 (xor_3_out, Add_Subtract, B[2]);
  and and_3 (and_3_out, B[2], A[2]);
  xor xor_4 (xor_4_out, Add_Subtract, B[3]);
  and and_4 (and_4_out, B[3], A[3]);
  not not_2 (not_2_out, xor_4_out);
  not not_3 (not_3_out, xor_5_out[3]);
  xor xor_5 (xor_5_out[0], xor_1_out, Add_Subtract);
  and and_5 (and_5_out, Add_Subtract, xor_1_out);
  xor xor_6 (xor_5_out[1], xor_2_out, or_1_out);
  and and_6 (and_6_out, or_1_out, xor_2_out);
  xor xor_7 (xor_5_out[2], xor_3_out, or_2_out);
  and and_7 (and_7_out, or_2_out, xor_3_out);
  xor xor_8 (xor_5_out[3], xor_4_out, or_3_out);
  and and_8 (and_8_out, or_3_out, xor_4_out);
  and and_9 (and_9_out, xor_5_out[3], not_2_out, not_1_out);
  and and_10 (and_10_out, not_3_out, xor_4_out, A[3]);
  or or_1 (or_1_out, and_5_out, and_1_out);
  or or_2 (or_2_out, and_6_out, and_2_out);
  or or_3 (or_3_out, and_7_out, and_3_out);
  or or_4 (or_4_out, and_8_out, and_4_out);
  or or_5 (or_5_out, and_9_out, and_10_out);
  LED C4 (.in(or_4_out));
  LED led_1 (.in(or_5_out));
  Hex_Digit_Display hex_digit_display_1 (.value(xor_5_out));  // open: dp
endmodule
