// Logisim project Q1.circ as structural Verilog: 3 circuits, main circuit main
module main (
  input  in_1,
  input  in_2,
  input  in_3,
  input  A,
  input  B,
  input  C,
  input  in_7,
  input  in_8,
  input  in_9,
  input  in_10,
  input  in_11,
  input  in_12,
  input  in_13,
  input  in_14,
  output out_15,
  output out_16,
  output out_17,
  output out_18,
  output out_19,
  output out_20,
  output out_21,
  output out_22,
  output out_23
);

  wire and_9_out, and_10_out, and_11_out, and_12_out, and_13_out, and_14_out, and_15_out, and_16_out,
       not_1_out, not_2_out, not_3_out, not_4_out, not_5_out, not_6_out;

  not not_1 (not_1_out, A);
  not not_2 (not_2_out, B);
  not not_3 (not_3_out, C);
  and and_1 (out_15, not_1_out, not_2_out, not_3_out);
  and and_2 (out_16, not_1_out, not_2_out, C);
  and and_3 (out_17, not_1_out, B, not_3_out);
  and and_4 (out_18, not_1_out, B, C);
  and and_5 (out_20, A, not_2_out, not_3_out);
  and and_6 (out_21, A, not_2_out, C);
  and and_7 (out_22, A, B, not_3_out);
  and and_8 (out_23, A, B, C);
  not not_4 (not_4_out, in_1);
  not not_5 (not_5_out, in_2);
  not not_6 (not_6_out, in_3);
  and and_9 (and_9_out, not_4_out, not_5_out, in_7, not_6_out);
  and and_10 (and_10_out, not_4_out, not_5_out, in_8, in_3);
  and and_11 (and_11_out, not_4_out, in_2, in_9, not_6_out);
  and and_12 (and_12_out, not_4_out, in_2, in_10, in_3);
  and and_13 (and_13_out, in_1, not_5_out, in_11, not_6_out);
  and and_14 (and_14_out, in_1, not_5_out, in_12, in_3);
  and and_15 (and_15_out, in_1, in_2, in_13, not_6_out);
  and and_16 (and_16_out, in_1, in_2, in_14, in_3);
  or or_1 (out_19, and_9_out, and_10_out, and_11_out, and_12_out, and_13_out, and_14_out, and_15_out, and_16_out);
endmodule

module Decoder38 (
  input  A,
  input  B,
  input  C,
  output out_4,
  output out_5,
  output out_6,
  output out_7,
  output out_8,
  output out_9,
  output out_10,
  output out_11
);

  wire not_1_out, not_2_out, not_3_out;

  not not_1 (not_1_out, A);
  not not_2 (not_2_out, B);
  not not_3 (not_3_out, C);
  and and_1 (out_4, not_1_out, not_2_out, not_3_out);
  and and_2 (out_5, not_1_out, not_2_out, C);
  and and_3 (out_6, not_1_out, B, not_3_out);
  and and_4 (out_7, not_1_out, B, C);
  and and_5 (out_8, A, not_2_out, not_3_out);
  and and_6 (out_9, A, not_2_out, C);
  and and_7 (out_10, A, B, not_3_out);
  and and_8 (out_11, A, B, C);
endmodule

module Multiplexer81 (
  input  in_1,
  input  in_2,
  input  in_3,
  input  in_4,
  input  in_5,
  input  in_6,
  input  in_7,
  input  in_8,
  input  in_9,
  input  in_10,
  input  in_11,
  output out_12
);

  wire and_1_out, and_2_out, and_3_out, and_4_out, and_5_out, and_6_out, and_7_out, and_8_out, not_1_out,
       not_2_out, not_3_out;

  not not_1 (not_1_out, in_1);
  not not_2 (not_2_out, in_2);
  not not_3 (not_3_out, in_3);
  and and_1 (and_1_out, not_1_out, not_2_out, in_4, not_3_out);
  and and_2 (and_2_out, not_1_out, not_2_out, in_5, in_3);
  and and_3 (and_3_out, not_1_out, in_2, in_6, not_3_out);
  and and_4 (and_4_out, not_1_out, in_2, in_7, in_3);
  and and_5 (and_5_out, in_1, not_2_out, in_8, not_3_out);
  and and_6 (and_6_out, in_1, not_2_out, in_9, in_3);
  and and_7 (and_7_out, in_1, in_2, in_10, not_3_out);
  and and_8 (and_8_out, in_1, in_2, in_11, in_3);
  or or_1 (out_12, and_1_out, and_2_out, and_3_out, and_4_out, and_5_out, and_6_out, and_7_out, and_8_out);
endmodule
