// Logisim project Q2.circ as structural Verilog: 3 circuits, main circuit main
module main (
  input  K0,
  input  K1,
  input  K2,
  input  K3,
  input  C0,
  input  C1,
  input  C2,
  input  C3,
  output L3,
  output L1,
  output L2
);

  wire comparater_1_agreaterthanb, comparater_1_alessthanb, encoder_1_x, encoder_1_y, encoder_2_x,
       encoder_2_y;

  Encoder encoder_1 (.A0(K0), .A1(K1), .A2(K2), .A3(K3), .X(encoder_1_x), .Y(encoder_1_y));
  Encoder encoder_2 (.A0(C0), .A1(C1), .A2(C2), .A3(C3), .X(encoder_2_x), .Y(encoder_2_y));
  Comparater comparater_1 (
    .A1(encoder_1_x), .A0(encoder_1_y), .B1(encoder_2_x), .B0(encoder_2_y), .AequalstoB(L3),
    .AlessthanB(comparater_1_alessthanb), .AgreaterthanB(comparater_1_agreaterthanb));
  or or_1 (L1, comparater_1_alessthanb, L3);
  or or_2 (L2, L3, comparater_1_agreaterthanb);

  // Notes on the sheet:
  //   K=C
  //   K<C
  //   K>c
endmodule

module Encoder (
  input  A0,
  input  A1,
  input  A2,
  input  A3,
  output X,
  output Y
);

  or or_1 (X, A2, A3);
  or or_2 (Y, A1, A3);
endmodule

module Comparater (
  input  A1,
  input  A0,
  input  B1,
  input  B0,
  output AequalstoB,
  output AlessthanB,
  output AgreaterthanB
);

  wire and_1_out, and_2_out, and_3_out, and_4_out, and_5_out, and_6_out, not_1_out, not_2_out, not_3_out,
       not_4_out, not_5_out, not_6_out, xor_1_out, xor_2_out;

  not not_1 (not_1_out, A1);
  not not_2 (not_2_out, A0);
  not not_3 (not_3_out, B1);
  and and_1 (and_1_out, not_1_out, B1);
  and and_2 (and_2_out, A1, not_3_out);
  not not_4 (not_4_out, B0);
  xor xor_1 (xor_1_out, A0, B0);
  not not_5 (not_5_out, xor_1_out);
  xor xor_2 (xor_2_out, A1, B1);
  not not_6 (not_6_out, xor_2_out);
  and and_3 (and_3_out, not_2_out, B0);
  and and_4 (and_4_out, A0, not_4_out);
  and and_5 (and_5_out, not_6_out, and_3_out);
  and and_6 (and_6_out, not_6_out, and_4_out);
  and and_7 (AequalstoB, not_5_out, not_6_out);
  or or_1 (AlessthanB, and_1_out, and_5_out);
  or or_2 (AgreaterthanB, and_2_out, and_6_out);
endmodule
