// Logisim project Universal_Shift_Register.circ as structural Verilog: 1 circuit, main circuit main
module main (
  input  D3,
  input  D2,
  input  D1,
  input  D0,
  input  SI_Right_Shift,
  input  SI_Left_Shift,
  input  S0,
  input  S1,
  input  Clear,
  output Q3,
  output Q2,
  output Q1,
  output Q0
);

  wire Clk_out, multiplexer_1_out, multiplexer_2_out, multiplexer_3_out, multiplexer_4_out;

  Clock Clk (.out(Clk_out));
  Multiplexer #(.select(2)) multiplexer_1 (
    .in0(D3), .in1(Q2), .in2(SI_Right_Shift), .in3(Q3), .out(multiplexer_1_out), .sel({S1, S0}));
  D_Flip_Flop d_ff_1 (.D(multiplexer_1_out), .clk(Clk_out), .Q(Q3), .reset(Clear));  // open: Qn, preset
  Multiplexer #(.select(2)) multiplexer_2 (
    .in0(D2), .in1(D1), .in2(Q3), .in3(Q2), .out(multiplexer_2_out), .sel({S1, S0}));
  D_Flip_Flop d_ff_2 (.D(multiplexer_2_out), .clk(Clk_out), .Q(Q2), .reset(Clear));  // open: Qn, preset
  Multiplexer #(.select(2)) multiplexer_3 (
    .in0(D1), .in1(Q0), .in2(Q2), .in3(D1), .out(multiplexer_3_out), .sel({S1, S0}));
  D_Flip_Flop d_ff_3 (.D(multiplexer_3_out), .clk(Clk_out), .Q(D1), .reset(Clear));  // open: Qn, preset
  Multiplexer #(.select(2)) multiplexer_4 (
    .in0(D0), .in1(SI_Left_Shift), .in2(D1), .in3(Q0), .out(multiplexer_4_out), .sel({S1, S0}));
  D_Flip_Flop d_ff_4 (.D(multiplexer_4_out), .clk(Clk_out), .Q(Q0), .reset(Clear));  // open: Qn, preset

  assign Q1 = D1;
endmodule
