// Logisim project GAME.circ as structural Verilog: 2 circuits, main circuit main
module main (
  input  in_1,
  input  in_2,
  input  in_3,
  input  in_4,
  output out_5,
  output out_6
);

  or or_1 (out_5, in_3, in_4);
  or or_2 (out_6, in_2, in_4);
endmodule

module ENCODE (
  input  in_1,
  input  in_2,
  input  in_3,
  input  in_4,
  input  in_5,
  input  in_6,
  input  in_7,
  input  in_8,
  output out_9,
  output out_10,
  output out_11
);

  wire and_1_out, and_2_out, and_4_out, main_1_out_5, main_1_out_6, main_2_out_5, main_2_out_6, not_1_out,
       not_2_out, not_3_out, not_4_out, or_1_out, or_2_out, xor_1_out, xor_2_out;

  main main_1 (.in_1(in_1), .in_2(in_2), .in_3(in_3), .in_4(in_4), .out_5(main_1_out_5), .out_6(main_1_out_6));
  main main_2 (.in_1(in_5), .in_2(in_6), .in_3(in_7), .in_4(in_8), .out_5(main_2_out_5), .out_6(main_2_out_6));
  and and_1 (and_1_out, main_1_out_5, main_2_out_5);
  xor xor_1 (xor_1_out, main_1_out_5, main_2_out_5);
  not not_1 (not_1_out, xor_1_out);
  xor xor_2 (xor_2_out, main_1_out_6, main_2_out_6);
  not not_2 (not_2_out, xor_2_out);
  not not_3 (not_3_out, main_2_out_6);
  and and_2 (and_2_out, main_1_out_6, not_3_out);
  and and_3 (out_9, not_1_out, not_2_out);
  or or_1 (or_1_out, and_1_out, and_2_out);
  and and_4 (and_4_out, main_2_out_6, not_4_out);
  not not_4 (not_4_out, main_1_out_6);
  or or_2 (or_2_out, and_1_out, and_4_out);
  or or_3 (out_11, or_2_out, out_9);
  or or_4 (out_10, or_1_out, out_9);
endmodule
