// Logisim project multiplexrer.circ as structural Verilog: 1 circuit, main circuit main
module main (
  input  C,
  input  A,
  input  B,
  output A1,
  output A2,
  output A3,
  output A4,
  output A5,
  output out_9,
  output out_10,
  output out_11
);

  wire not_1_out, not_2_out, not_3_out;

  not not_1 (not_1_out, A);
  not not_2 (not_2_out, B);
  not not_3 (not_3_out, C);
  and and_1 (A1, not_1_out, not_2_out, not_3_out);
  and and_2 (A2, not_1_out, not_2_out, C);
  and and_3 (A3, not_1_out, B, not_3_out);
  and and_4 (A4, not_1_out, B, C);
  and and_5 (A5, A, not_2_out, not_3_out);
  and and_6 (out_9, A, not_2_out, C);
  and and_7 (out_10, A, B, not_3_out);
  and and_8 (out_11, A, B, C);

  // Notes on the sheet:
  //   A6
  //   A7
  //   A8
endmodule
