// Logisim project GRAY_TO_BINARY.circ as structural Verilog: 1 circuit, main circuit main
module main (
  input  G3,
  input  G2,
  input  G1,
  input  G0,
  output B3,
  output B2,
  output B1,
  output B0
);

  xor xor_1 (B2, G3, G2);
  xor xor_2 (B1, B2, G1);
  xor xor_3 (B0, B1, G0);
  Hex_Digit_Display hex_digit_display_1 (.value({B0, B1, B2, G3}));  // open: dp

  assign B3 = G3;
endmodule
