// Logisim project CLA.circ as structural Verilog: 2 circuits, main circuit main
module main (
  input  [3:0] A,
  input  [3:0] B,
  input  in_3,
  output s0,
  output s1,
  output s2,
  output s3,
  output s4
);

  wire and_1_out, and_2_out, and_3_out, and_4_out, and_5_out, and_6_out, or_1_out, or_2_out, xor_1_out,
       xor_2_out;

  and and_1 (and_1_out, A[1], B[1]);
  xor xor_1 (xor_1_out, A[2], B[2]);
  and and_2 (and_2_out, A[2], B[2]);
  xor xor_2 (xor_2_out, A[3], B[3]);
  and and_3 (and_3_out, and_1_out, xor_1_out);
  and and_4 (and_4_out, xor_1_out, and_1_out, xor_2_out);
  and and_5 (and_5_out, xor_2_out, and_2_out);
  and and_6 (and_6_out, A[3], B[3]);
  or or_1 (or_1_out, and_3_out, and_2_out);
  or or_2 (or_2_out, and_4_out, and_5_out, and_6_out);
  fulladd fulladd_1 (.A(A[0]), .B(B[0]), .C_IN(in_3), .S(s0));  // open: COUT
  fulladd fulladd_2 (.A(A[1]), .B(B[1]), .C_IN(and_1_out), .S(s1));  // open: COUT
  fulladd fulladd_3 (.A(A[2]), .B(B[2]), .C_IN(or_1_out), .S(s2));  // open: COUT
  fulladd fulladd_4 (.A(A[3]), .B(B[3]), .C_IN(or_2_out), .S(s3), .COUT(s4));
endmodule

module fulladd (
  input  A,
  input  B,
  input  C_IN,
  output S,
  output COUT
);

  wire and_1_out, and_2_out, xor_2_out;

  xor xor_1 (S, A, B, C_IN);
  xor xor_2 (xor_2_out, A, B);
  and and_1 (and_1_out, B, A);
  and and_2 (and_2_out, xor_2_out, C_IN);
  or or_1 (COUT, and_2_out, and_1_out);
endmodule
