// Logisim project UNIVERSAL.circ as structural Verilog
module universal_shift_register (
  input  LEFT_SHIFT_BIT,
  input  RIGHT_SHIFT_BIT,
  input  I0,
  input  I1,
  input  I2,
  input  I3,
  input  [1:0] SELECTION_BITS,
  output [3:0] OUT_4BIT
);

  wire clock_1_out, multiplexer_1_out, multiplexer_2_out, multiplexer_3_out, multiplexer_4_out;

  D_Flip_Flop d_ff_1 (.D(multiplexer_1_out), .clk(clock_1_out), .Q(OUT_4BIT[3]));  // open: Qn, preset, reset
  Clock clock_1 (.out(clock_1_out));
  Multiplexer #(.select(2)) multiplexer_1 (
    .in0(RIGHT_SHIFT_BIT), .in1(OUT_4BIT[2]), .in2(I0), .in3(OUT_4BIT[3]), .out(multiplexer_1_out),
    .sel(SELECTION_BITS));
  D_Flip_Flop d_ff_2 (.D(multiplexer_2_out), .clk(clock_1_out), .Q(OUT_4BIT[2]));  // open: Qn, preset, reset
  Multiplexer #(.select(2)) multiplexer_2 (
    .in0(OUT_4BIT[3]), .in1(OUT_4BIT[1]), .in2(I1), .in3(OUT_4BIT[2]), .out(multiplexer_2_out),
    .sel(SELECTION_BITS));
  Multiplexer #(.select(2)) multiplexer_3 (
    .in0(OUT_4BIT[2]), .in1(OUT_4BIT[0]), .in2(I2), .in3(OUT_4BIT[1]), .out(multiplexer_3_out),
    .sel(SELECTION_BITS));
  D_Flip_Flop d_ff_3 (.D(multiplexer_3_out), .clk(clock_1_out), .Q(OUT_4BIT[1]));  // open: Qn, preset, reset
  D_Flip_Flop d_ff_4 (.D(multiplexer_4_out), .clk(clock_1_out), .Q(OUT_4BIT[0]));  // open: Qn, preset, reset
  Multiplexer #(.select(2)) multiplexer_4 (
    .in0(OUT_4BIT[1]), .in1(LEFT_SHIFT_BIT), .in2(I3), .in3(OUT_4BIT[0]), .out(multiplexer_4_out),
    .sel(SELECTION_BITS));
endmodule
