// Logisim project ALL_SEQ.circ as structural Verilog
module Upcounter_4bit (
  input  D,
  input  RESET,
  input  in_3,
  input  in_4,
  output out_5,
  output out_6,
  output out_7,
  output out_8
);

  wire and_1_out, clock_1_out;
  wire [3:0] j_k_ff_1_q;

  Clock clock_1 (.out(clock_1_out));
  and and_1 (and_1_out, j_k_ff_1_q[0], j_k_ff_1_q[1], j_k_ff_1_q[2], j_k_ff_1_q[3]);
  J_K_Flip_Flop #(.trigger("falling")) j_k_ff_1 (
    .J(D), .K(D), .clk(clock_1_out), .Q(j_k_ff_1_q[0]), .reset(RESET));  // open: Qn, preset
  J_K_Flip_Flop #(.trigger("falling")) j_k_ff_2 (
    .J(in_3), .K(in_3), .clk(and_1_out), .Q(out_5), .reset(in_4));  // open: Qn, preset
  J_K_Flip_Flop #(.trigger("falling")) j_k_ff_3 (
    .J(in_3), .K(in_3), .clk(out_5), .Q(out_6), .reset(in_4));  // open: Qn, preset
  J_K_Flip_Flop #(.trigger("falling")) j_k_ff_4 (
    .J(D), .K(D), .clk(j_k_ff_1_q[0]), .Q(j_k_ff_1_q[1]), .reset(RESET));  // open: Qn, preset
  J_K_Flip_Flop #(.trigger("falling")) j_k_ff_5 (
    .J(D), .K(D), .clk(j_k_ff_1_q[1]), .Q(j_k_ff_1_q[2]), .reset(RESET));  // open: Qn, preset
  J_K_Flip_Flop #(.trigger("falling")) j_k_ff_6 (
    .J(in_3), .K(in_3), .clk(out_6), .Q(out_7), .reset(in_4));  // open: Qn, preset
  J_K_Flip_Flop #(.trigger("falling")) j_k_ff_7 (
    .J(D), .K(D), .clk(j_k_ff_1_q[2]), .Q(j_k_ff_1_q[3]), .reset(RESET));  // open: Qn, preset
  J_K_Flip_Flop #(.trigger("falling")) j_k_ff_8 (
    .J(in_3), .K(in_3), .clk(out_7), .Q(out_8), .reset(in_4));  // open: Qn, preset
  Hex_Digit_Display hex_digit_display_1 (.value(j_k_ff_1_q));  // open: dp
  Hex_Digit_Display hex_digit_display_2 (.value({out_8, out_7, out_6, out_5}));  // open: dp
endmodule

module Downcounter_4bit (
  input  in_1,
  input  in_2
);

  wire clock_1_out, j_k_ff_1_q, j_k_ff_2_q, j_k_ff_3_q;
  wire [3:0] j_k_ff_1_qn;

  Clock clock_1 (.out(clock_1_out));
  J_K_Flip_Flop #(.trigger("falling")) j_k_ff_1 (
    .J(in_1), .K(in_1), .clk(clock_1_out), .Q(j_k_ff_1_q), .Qn(j_k_ff_1_qn[0]), .reset(in_2));  // open: preset
  J_K_Flip_Flop #(.trigger("falling")) j_k_ff_2 (
    .J(in_1), .K(in_1), .clk(j_k_ff_1_q), .Q(j_k_ff_2_q), .Qn(j_k_ff_1_qn[1]), .reset(in_2));  // open: preset
  J_K_Flip_Flop #(.trigger("falling")) j_k_ff_3 (
    .J(in_1), .K(in_1), .clk(j_k_ff_2_q), .Q(j_k_ff_3_q), .Qn(j_k_ff_1_qn[2]), .reset(in_2));  // open: preset
  J_K_Flip_Flop #(.trigger("falling")) j_k_ff_4 (
    .J(in_1), .K(in_1), .clk(j_k_ff_3_q), .Qn(j_k_ff_1_qn[3]), .reset(in_2));  // open: Q, preset
  Hex_Digit_Display hex_digit_display_1 (.value(j_k_ff_1_qn));  // open: dp
endmodule

module Up_Down_counter_4bit (
  input  in_1,
  input  in_2,
  input  in_3
);

  wire clock_1_out, j_k_ff_1_q, j_k_ff_1_qn, j_k_ff_2_q, j_k_ff_2_qn, j_k_ff_3_q, j_k_ff_3_qn, j_k_ff_4_q,
       j_k_ff_4_qn;
  wire [3:0] multiplexer_1_out;

  Clock clock_1 (.out(clock_1_out));
  J_K_Flip_Flop #(.trigger("falling")) j_k_ff_1 (
    .J(in_1), .K(in_1), .clk(clock_1_out), .Q(j_k_ff_1_q), .Qn(j_k_ff_1_qn), .reset(in_2));  // open: preset
  J_K_Flip_Flop #(.trigger("falling")) j_k_ff_2 (
    .J(in_1), .K(in_1), .clk(j_k_ff_1_q), .Q(j_k_ff_2_q), .Qn(j_k_ff_2_qn), .reset(in_2));  // open: preset
  Multiplexer multiplexer_1 (.in0(j_k_ff_1_q), .in1(j_k_ff_1_qn), .out(multiplexer_1_out[0]), .sel(in_3));
  J_K_Flip_Flop #(.trigger("falling")) j_k_ff_3 (
    .J(in_1), .K(in_1), .clk(j_k_ff_2_q), .Q(j_k_ff_3_q), .Qn(j_k_ff_3_qn), .reset(in_2));  // open: preset
  Multiplexer multiplexer_2 (.in0(j_k_ff_2_q), .in1(j_k_ff_2_qn), .out(multiplexer_1_out[1]), .sel(in_3));
  J_K_Flip_Flop #(.trigger("falling")) j_k_ff_4 (
    .J(in_1), .K(in_1), .clk(j_k_ff_3_q), .Q(j_k_ff_4_q), .Qn(j_k_ff_4_qn), .reset(in_2));  // open: preset
  Multiplexer multiplexer_3 (.in0(j_k_ff_3_q), .in1(j_k_ff_3_qn), .out(multiplexer_1_out[2]), .sel(in_3));
  Multiplexer multiplexer_4 (.in0(j_k_ff_4_q), .in1(j_k_ff_4_qn), .out(multiplexer_1_out[3]), .sel(in_3));
  Hex_Digit_Display hex_digit_display_1 (.value(multiplexer_1_out));  // open: dp
endmodule

module right_shift_registers (
  input  in_1,
  output [3:0] out_2
);

  wire clock_1_out;

  Clock clock_1 (.out(clock_1_out));
  D_Flip_Flop d_ff_1 (.D(in_1), .clk(clock_1_out), .Q(out_2[0]));  // open: Qn, preset, reset
  D_Flip_Flop d_ff_2 (.D(out_2[0]), .clk(clock_1_out), .Q(out_2[1]));  // open: Qn, preset, reset
  D_Flip_Flop d_ff_3 (.D(out_2[1]), .clk(clock_1_out), .Q(out_2[2]));  // open: Qn, preset, reset
  D_Flip_Flop d_ff_4 (.D(out_2[2]), .clk(clock_1_out), .Q(out_2[3]));  // open: Qn, preset, reset
endmodule

module right_left_shift_register (
  input  in_1,
  input  in_2,
  input  in_3,
  output [3:0] out_4
);

  wire clock_1_out, multiplexer_1_out, multiplexer_2_out, multiplexer_3_out, multiplexer_4_out;

  Clock clock_1 (.out(clock_1_out));
  Multiplexer multiplexer_1 (.in0(in_2), .in1(out_4[1]), .out(multiplexer_1_out), .sel(in_1));
  D_Flip_Flop d_ff_1 (.D(multiplexer_1_out), .clk(clock_1_out), .Q(out_4[0]));  // open: Qn, preset, reset
  Multiplexer multiplexer_2 (.in0(out_4[0]), .in1(out_4[2]), .out(multiplexer_2_out), .sel(in_1));
  D_Flip_Flop d_ff_2 (.D(multiplexer_2_out), .clk(clock_1_out), .Q(out_4[1]));  // open: Qn, preset, reset
  Multiplexer multiplexer_3 (.in0(out_4[1]), .in1(out_4[3]), .out(multiplexer_3_out), .sel(in_1));
  D_Flip_Flop d_ff_3 (.D(multiplexer_3_out), .clk(clock_1_out), .Q(out_4[2]));  // open: Qn, preset, reset
  D_Flip_Flop d_ff_4 (.D(multiplexer_4_out), .clk(clock_1_out), .Q(out_4[3]));  // open: Qn, preset, reset
  Multiplexer multiplexer_4 (.in0(out_4[2]), .in1(in_3), .out(multiplexer_4_out), .sel(in_1));
endmodule

module left_shift_register (
  input  in_1,
  output [3:0] out_2
);

  wire clock_1_out;

  Clock clock_1 (.out(clock_1_out));
  D_Flip_Flop d_ff_1 (.D(out_2[1]), .clk(clock_1_out), .Q(out_2[0]));  // open: Qn, preset, reset
  D_Flip_Flop d_ff_2 (.D(out_2[2]), .clk(clock_1_out), .Q(out_2[1]));  // open: Qn, preset, reset
  D_Flip_Flop d_ff_3 (.D(out_2[3]), .clk(clock_1_out), .Q(out_2[2]));  // open: Qn, preset, reset
  D_Flip_Flop d_ff_4 (.D(in_1), .clk(clock_1_out), .Q(out_2[3]));  // open: Qn, preset, reset
endmodule

module parallel_input_shift_register (
  input  in_1,
  input  in_2,
  input  in_3,
  input  in_4,
  input  in_5,
  input  in_6,
  input  in_7,
  output [3:0] out_8
);

  wire clock_1_out, multiplexer_1_out, multiplexer_2_out, multiplexer_3_out, multiplexer_4_out;

  Clock clock_1 (.out(clock_1_out));
  Multiplexer multiplexer_1 (.in0(in_2), .in1(in_3), .out(multiplexer_1_out), .sel(in_1));
  D_Flip_Flop d_ff_1 (.D(multiplexer_1_out), .clk(clock_1_out), .Q(out_8[0]), .reset(in_7));  // open: Qn, preset
  Multiplexer multiplexer_2 (.in0(out_8[0]), .in1(in_4), .out(multiplexer_2_out), .sel(in_1));
  D_Flip_Flop d_ff_2 (.D(multiplexer_2_out), .clk(clock_1_out), .Q(out_8[1]), .reset(in_7));  // open: Qn, preset
  Multiplexer multiplexer_3 (.in0(out_8[1]), .in1(in_5), .out(multiplexer_3_out), .sel(in_1));
  D_Flip_Flop d_ff_3 (.D(multiplexer_3_out), .clk(clock_1_out), .Q(out_8[2]), .reset(in_7));  // open: Qn, preset
  Multiplexer multiplexer_4 (.in0(out_8[2]), .in1(in_6), .out(multiplexer_4_out), .sel(in_1));
  D_Flip_Flop d_ff_4 (.D(multiplexer_4_out), .clk(clock_1_out), .Q(out_8[3]), .reset(in_7));  // open: Qn, preset
endmodule

module universal_shift_register (
  input  in_1,
  input  in_2,
  input  in_3,
  input  in_4,
  input  in_5,
  input  in_6,
  input  [1:0] in_7,
  output [3:0] out_8
);

  wire clock_1_out, multiplexer_1_out, multiplexer_2_out, multiplexer_3_out, multiplexer_4_out;

  D_Flip_Flop d_ff_1 (.D(multiplexer_1_out), .clk(clock_1_out), .Q(out_8[0]));  // open: Qn, preset, reset
  Clock clock_1 (.out(clock_1_out));
  Multiplexer #(.select(2)) multiplexer_1 (
    .in0(in_1), .in1(out_8[1]), .in2(in_2), .in3(out_8[0]), .out(multiplexer_1_out), .sel(in_7));
  D_Flip_Flop d_ff_2 (.D(multiplexer_2_out), .clk(clock_1_out), .Q(out_8[1]));  // open: Qn, preset, reset
  Multiplexer #(.select(2)) multiplexer_2 (
    .in0(out_8[0]), .in1(out_8[2]), .in2(in_3), .in3(out_8[1]), .out(multiplexer_2_out), .sel(in_7));
  Multiplexer #(.select(2)) multiplexer_3 (
    .in0(out_8[1]), .in1(out_8[3]), .in2(in_4), .in3(out_8[2]), .out(multiplexer_3_out), .sel(in_7));
  D_Flip_Flop d_ff_3 (.D(multiplexer_3_out), .clk(clock_1_out), .Q(out_8[2]));  // open: Qn, preset, reset
  D_Flip_Flop d_ff_4 (.D(multiplexer_4_out), .clk(clock_1_out), .Q(out_8[3]));  // open: Qn, preset, reset
  Multiplexer #(.select(2)) multiplexer_4 (
    .in0(out_8[2]), .in1(in_5), .in2(in_6), .in3(out_8[3]), .out(multiplexer_4_out), .sel(in_7));
endmodule

module serial_input_parallel_out_register (
  input  in_1,
  output [3:0] out_2
);

  wire clock_1_out;

  Clock clock_1 (.out(clock_1_out));
  D_Flip_Flop d_ff_1 (.D(in_1), .clk(clock_1_out), .Q(out_2[0]));  // open: Qn, preset, reset
  D_Flip_Flop d_ff_2 (.D(out_2[0]), .clk(clock_1_out), .Q(out_2[1]));  // open: Qn, preset, reset
  D_Flip_Flop d_ff_3 (.D(out_2[1]), .clk(clock_1_out), .Q(out_2[2]));  // open: Qn, preset, reset
  D_Flip_Flop d_ff_4 (.D(out_2[2]), .clk(clock_1_out), .Q(out_2[3]));  // open: Qn, preset, reset
endmodule

module ring_counter (
  input  in_1,
  output [3:0] out_2
);

  wire clock_1_out;

  Clock clock_1 (.out(clock_1_out));
  D_Flip_Flop #(.trigger("falling")) d_ff_1 (
    .D(out_2[0]), .clk(clock_1_out), .Q(out_2[3]), .preset(in_1));  // open: Qn, reset
  D_Flip_Flop #(.trigger("falling")) d_ff_2 (
    .D(out_2[3]), .clk(clock_1_out), .Q(out_2[2]), .reset(in_1));  // open: Qn, preset
  D_Flip_Flop #(.trigger("falling")) d_ff_3 (
    .D(out_2[2]), .clk(clock_1_out), .Q(out_2[1]), .reset(in_1));  // open: Qn, preset
  D_Flip_Flop #(.trigger("falling")) d_ff_4 (
    .D(out_2[1]), .clk(clock_1_out), .Q(out_2[0]), .reset(in_1));  // open: Qn, preset
endmodule

module jenson_counter (
  input  in_1,
  output [3:0] out_2
);

  wire clock_1_out, d_ff_4_qn;

  Clock clock_1 (.out(clock_1_out));
  D_Flip_Flop #(.trigger("falling")) d_ff_1 (
    .D(d_ff_4_qn), .clk(clock_1_out), .Q(out_2[3]), .reset(in_1));  // open: Qn, preset
  D_Flip_Flop #(.trigger("falling")) d_ff_2 (
    .D(out_2[3]), .clk(clock_1_out), .Q(out_2[2]), .reset(in_1));  // open: Qn, preset
  D_Flip_Flop #(.trigger("falling")) d_ff_3 (
    .D(out_2[2]), .clk(clock_1_out), .Q(out_2[1]), .reset(in_1));  // open: Qn, preset
  D_Flip_Flop #(.trigger("falling")) d_ff_4 (
    .D(out_2[1]), .clk(clock_1_out), .Q(out_2[0]), .Qn(d_ff_4_qn), .reset(in_1));  // open: preset
endmodule
